// Logisim project cpu21-riscv-multi-level-interrupt-software-stack.circ as structural Verilog: 7 circuits, main circuit ◆单周期硬布线控制器
// 单周期硬布线控制器
module \单周期硬布线控制器  (
  input  [4:0] OP,
  input  [4:0] Funct,
  input  IR21,
  output [3:0] ALU_OP,
  output uret,
  output ecall,
  output MemToReg,
  output MemWrite,
  output ALU_SRC,
  output RegWrite,
  output S_type,
  output Beq,
  output Bne,
  output Jalr,
  output JAL,
  output Lui,
  output Lbu,
  output Bge,
  output csrrsi,
  output csrrci,
  output csrrw
);

  wire not_1_out, \控制信号自动生成_1_ecall ;

  \运算控制器自动生成  \u_运算控制器自动生成_1  (
    .OP2(OP[0]), .OP3(OP[1]), .OP4(OP[2]), .OP5(OP[3]), .OP6(OP[4]), .F12(Funct[0]), .F13(Funct[1]),
    .F14(Funct[2]), .F25(Funct[3]), .F30(Funct[4]), .S0(ALU_OP[0]), .S1(ALU_OP[1]), .S2(ALU_OP[2]),
    .S3(ALU_OP[3]));
  \控制信号自动生成  \u_控制信号自动生成_1  (
    .OP2(OP[0]), .OP3(OP[1]), .OP4(OP[2]), .OP5(OP[3]), .OP6(OP[4]), .MemToReg(MemToReg), .F12(Funct[0]),
    .F13(Funct[1]), .F14(Funct[2]), .F25(Funct[3]), .F30(Funct[4]), .MemWrite(MemWrite), .ALU_SRC(ALU_SRC),
    .RegWrite(RegWrite), .ecall(\控制信号自动生成_1_ecall ), .S_Type(S_type), .BEQ(Beq), .BNE(Bne), .JALR(Jalr),
    .JAL(JAL), .LUI(Lui), .LBU(Lbu), .BGE(Bge), .CSRRSI(csrrsi), .CSRRCI(csrrci), .CSRRW(csrrw));
  not not_1 (not_1_out, IR21);
  and and_1 (uret, IR21, \控制信号自动生成_1_ecall );
  and and_2 (ecall, not_1_out, \控制信号自动生成_1_ecall );

  // Other names for the same wires on the sheet: OP_CODE[4:0] = OP

  // Notes on the sheet:
  //   运算器控制器，根据指令生成运算器功能选择信号
  //   控制信号生成，产生数据通路需要的其他控制信号
endmodule

// 运算器控制器
module \运算控制器自动生成  (
  input  OP2,
  input  OP3,
  input  OP4,
  input  OP5,
  input  OP6,
  input  F12,
  input  F13,
  input  F14,
  input  F25,
  input  F30,
  output S0,
  output S1,
  output S2,
  output S3
);

  wire and_1_out, and_2_out, and_3_out, and_4_out, and_5_out, and_6_out, and_7_out, and_8_out, and_9_out,
       and_10_out, and_11_out, and_12_out, and_13_out, and_14_out, and_15_out, and_16_out, and_17_out,
       and_18_out, and_19_out, and_20_out, and_21_out, and_22_out, and_23_out, not_1_out, not_2_out,
       not_3_out, not_4_out, not_5_out, not_6_out, not_7_out, not_8_out, not_9_out, not_10_out, not_11_out,
       not_12_out, not_13_out, not_14_out, not_15_out, not_16_out, not_17_out, not_18_out, not_19_out,
       not_20_out, not_21_out, not_22_out, not_23_out, not_24_out, not_25_out, not_26_out, not_27_out,
       not_28_out, not_29_out, not_30_out, not_31_out, not_32_out, not_33_out, not_34_out, not_35_out,
       not_36_out, not_37_out, not_38_out, not_39_out, not_40_out, not_41_out, not_42_out, not_43_out,
       not_44_out, not_45_out, not_46_out, not_47_out, not_48_out, not_49_out, not_50_out, not_51_out,
       not_52_out, not_53_out, not_54_out, not_55_out, not_56_out, not_57_out, not_58_out, not_59_out,
       not_60_out, not_61_out, not_62_out, not_63_out, not_64_out, not_65_out, not_66_out, not_67_out,
       not_68_out, not_69_out, not_70_out, not_71_out, not_72_out, not_73_out, not_74_out, not_75_out,
       not_76_out, not_77_out, not_78_out, not_79_out, not_80_out, not_81_out, not_82_out, not_83_out,
       not_84_out, not_85_out, not_86_out, not_87_out, not_88_out, not_89_out, not_90_out, not_91_out,
       not_92_out, not_93_out, not_94_out, not_95_out, not_96_out, not_97_out, not_98_out, not_99_out,
       not_100_out, not_101_out, not_102_out, not_103_out, not_104_out, not_105_out, not_106_out,
       not_107_out, not_108_out, not_109_out, not_110_out, not_111_out, not_112_out, not_113_out,
       not_114_out, not_115_out, not_116_out, not_117_out, not_118_out, not_119_out, not_120_out,
       not_121_out, not_122_out, not_123_out, not_124_out, not_125_out, not_126_out, not_127_out,
       not_128_out, not_129_out, not_130_out, not_131_out, not_132_out, not_133_out;

  not not_1 (not_1_out, OP2);
  not not_2 (not_2_out, OP3);
  not not_3 (not_3_out, OP4);
  not not_4 (not_4_out, OP6);
  not not_5 (not_5_out, F12);
  not not_6 (not_6_out, F14);
  not not_7 (not_7_out, OP2);
  not not_8 (not_8_out, OP3);
  not not_9 (not_9_out, OP5);
  not not_10 (not_10_out, OP6);
  not not_11 (not_11_out, F12);
  not not_12 (not_12_out, F13);
  not not_13 (not_13_out, OP2);
  not not_14 (not_14_out, OP3);
  not not_15 (not_15_out, OP5);
  not not_16 (not_16_out, OP6);
  not not_17 (not_17_out, F12);
  not not_18 (not_18_out, F14);
  not not_19 (not_19_out, OP2);
  not not_20 (not_20_out, OP3);
  not not_21 (not_21_out, OP6);
  not not_22 (not_22_out, F12);
  not not_23 (not_23_out, F13);
  not not_24 (not_24_out, F25);
  not not_25 (not_25_out, F30);
  not not_26 (not_26_out, OP2);
  not not_27 (not_27_out, OP3);
  not not_28 (not_28_out, OP6);
  not not_29 (not_29_out, F12);
  not not_30 (not_30_out, F14);
  not not_31 (not_31_out, F25);
  not not_32 (not_32_out, F30);
  not not_33 (not_33_out, OP2);
  not not_34 (not_34_out, OP3);
  not not_35 (not_35_out, OP5);
  not not_36 (not_36_out, OP6);
  not not_37 (not_37_out, F13);
  not not_38 (not_38_out, F25);
  not not_39 (not_39_out, OP2);
  not not_40 (not_40_out, OP3);
  not not_41 (not_41_out, OP5);
  not not_42 (not_42_out, OP6);
  not not_43 (not_43_out, OP2);
  not not_44 (not_44_out, OP3);
  not not_45 (not_45_out, OP6);
  not not_46 (not_46_out, F25);
  not not_47 (not_47_out, F30);
  not not_48 (not_48_out, OP2);
  not not_49 (not_49_out, OP3);
  not not_50 (not_50_out, OP5);
  not not_51 (not_51_out, OP6);
  not not_52 (not_52_out, F12);
  not not_53 (not_53_out, F14);
  not not_54 (not_54_out, OP2);
  not not_55 (not_55_out, OP3);
  not not_56 (not_56_out, OP6);
  not not_57 (not_57_out, F12);
  not not_58 (not_58_out, F14);
  not not_59 (not_59_out, F25);
  not not_60 (not_60_out, F30);
  not not_61 (not_61_out, OP2);
  not not_62 (not_62_out, OP3);
  not not_63 (not_63_out, OP5);
  not not_64 (not_64_out, OP6);
  not not_65 (not_65_out, F25);
  not not_66 (not_66_out, F30);
  not not_67 (not_67_out, OP2);
  not not_68 (not_68_out, OP3);
  not not_69 (not_69_out, OP5);
  not not_70 (not_70_out, OP6);
  not not_71 (not_71_out, OP2);
  not not_72 (not_72_out, OP3);
  not not_73 (not_73_out, OP6);
  not not_74 (not_74_out, F25);
  not not_75 (not_75_out, F30);
  not not_76 (not_76_out, OP2);
  not not_77 (not_77_out, OP3);
  not not_78 (not_78_out, OP6);
  not not_79 (not_79_out, F12);
  not not_80 (not_80_out, F13);
  not not_81 (not_81_out, F14);
  not not_82 (not_82_out, F25);
  not not_83 (not_83_out, OP2);
  not not_84 (not_84_out, OP3);
  not not_85 (not_85_out, OP4);
  not not_86 (not_86_out, OP6);
  not not_87 (not_87_out, F12);
  not not_88 (not_88_out, F14);
  not not_89 (not_89_out, OP2);
  not not_90 (not_90_out, OP3);
  not not_91 (not_91_out, OP5);
  not not_92 (not_92_out, OP6);
  not not_93 (not_93_out, F12);
  not not_94 (not_94_out, F13);
  not not_95 (not_95_out, F14);
  not not_96 (not_96_out, OP2);
  not not_97 (not_97_out, OP3);
  not not_98 (not_98_out, OP6);
  not not_99 (not_99_out, F12);
  not not_100 (not_100_out, F13);
  not not_101 (not_101_out, F14);
  not not_102 (not_102_out, F25);
  not not_103 (not_103_out, OP2);
  not not_104 (not_104_out, OP3);
  not not_105 (not_105_out, OP5);
  not not_106 (not_106_out, OP6);
  not not_107 (not_107_out, OP2);
  not not_108 (not_108_out, OP3);
  not not_109 (not_109_out, OP6);
  not not_110 (not_110_out, F25);
  not not_111 (not_111_out, F30);
  not not_112 (not_112_out, OP2);
  not not_113 (not_113_out, OP3);
  not not_114 (not_114_out, OP5);
  not not_115 (not_115_out, OP6);
  not not_116 (not_116_out, F12);
  not not_117 (not_117_out, OP2);
  not not_118 (not_118_out, OP3);
  not not_119 (not_119_out, OP6);
  not not_120 (not_120_out, F12);
  not not_121 (not_121_out, F25);
  not not_122 (not_122_out, F30);
  not not_123 (not_123_out, OP2);
  not not_124 (not_124_out, OP3);
  not not_125 (not_125_out, OP5);
  not not_126 (not_126_out, OP6);
  not not_127 (not_127_out, F12);
  not not_128 (not_128_out, OP2);
  not not_129 (not_129_out, OP3);
  not not_130 (not_130_out, OP6);
  not not_131 (not_131_out, F14);
  not not_132 (not_132_out, F25);
  not not_133 (not_133_out, F30);
  and and_1 (and_1_out, not_1_out, not_2_out, not_3_out, not_4_out, not_5_out, F13, not_6_out);
  and and_2 (and_2_out, not_7_out, not_8_out, OP4, not_9_out, not_10_out, not_11_out, not_12_out);
  and and_3 (and_3_out, not_13_out, not_14_out, OP4, not_15_out, not_16_out, not_17_out, not_18_out);
  and and_4 (and_4_out, not_19_out, not_20_out, OP4, not_21_out, not_22_out, not_23_out, not_24_out, not_25_out);
  and and_5 (and_5_out, not_26_out, not_27_out, OP4, not_28_out, not_29_out, not_30_out, not_31_out, not_32_out);
  and and_6 (and_6_out, not_33_out, not_34_out, OP4, not_35_out, not_36_out, not_37_out, F14, not_38_out, F30);
  and and_7 (and_7_out, not_39_out, not_40_out, OP4, not_41_out, not_42_out, F12, F13, F14);
  and and_8 (and_8_out, not_43_out, not_44_out, OP4, not_45_out, F12, F13, F14, not_46_out, not_47_out);
  and and_9 (and_9_out, not_48_out, not_49_out, OP4, not_50_out, not_51_out, not_52_out, F13, not_53_out);
  and and_10 (and_10_out, not_54_out, not_55_out, OP4, not_56_out, not_57_out, F13, not_58_out, not_59_out, not_60_out);
  and and_11 (and_11_out, not_61_out, not_62_out, OP4, not_63_out, not_64_out, F12, F14, not_65_out, not_66_out);
  and and_12 (and_12_out, not_67_out, not_68_out, OP4, not_69_out, not_70_out, F12, F13, F14);
  and and_13 (and_13_out, not_71_out, not_72_out, OP4, not_73_out, F12, F13, F14, not_74_out, not_75_out);
  and and_14 (and_14_out, not_76_out, not_77_out, OP4, OP5, not_78_out, not_79_out, not_80_out, not_81_out, not_82_out, F30);
  and and_15 (and_15_out, not_83_out, not_84_out, not_85_out, not_86_out, not_87_out, F13, not_88_out);
  and and_16 (and_16_out, not_89_out, not_90_out, OP4, not_91_out, not_92_out, not_93_out, not_94_out, not_95_out);
  and and_17 (and_17_out, not_96_out, not_97_out, OP4, not_98_out, not_99_out, not_100_out, not_101_out, not_102_out);
  and and_18 (and_18_out, not_103_out, not_104_out, OP4, not_105_out, not_106_out, F12, F13, F14);
  and and_19 (and_19_out, not_107_out, not_108_out, OP4, OP5, not_109_out, F12, F13, not_110_out, not_111_out);
  and and_20 (and_20_out, not_112_out, not_113_out, OP4, not_114_out, not_115_out, not_116_out, F14);
  and and_21 (and_21_out, not_117_out, not_118_out, OP4, not_119_out, not_120_out, F14, not_121_out, not_122_out);
  and and_22 (and_22_out, not_123_out, not_124_out, OP4, not_125_out, not_126_out, not_127_out, F13);
  and and_23 (and_23_out, not_128_out, not_129_out, OP4, OP5, not_130_out, F13, not_131_out, not_132_out, not_133_out);
  or or_1 (S2, and_15_out, and_16_out, and_17_out, and_18_out, and_19_out);
  or or_2 (S3, and_20_out, and_21_out, and_22_out, and_23_out);
  or or_3 (S0, and_1_out, and_2_out, and_3_out, and_4_out, and_5_out, and_6_out, and_7_out, and_8_out);
  or or_4 (S1, and_9_out, and_10_out, and_11_out, and_12_out, and_13_out, and_14_out);
endmodule

// 控制信号生成
module \控制信号自动生成  (
  input  OP2,
  input  OP3,
  input  OP4,
  input  OP5,
  input  OP6,
  input  F12,
  input  F13,
  input  F14,
  input  F25,
  input  F30,
  output MemToReg,
  output MemWrite,
  output ALU_SRC,
  output RegWrite,
  output ecall,
  output S_Type,
  output BEQ,
  output BNE,
  output JALR,
  output JAL,
  output LUI,
  output LBU,
  output BGE,
  output CSRRSI,
  output CSRRCI,
  output CSRRW
);

  wire and_1_out, and_2_out, and_4_out, and_5_out, and_6_out, and_7_out, and_8_out, and_9_out, and_10_out,
       and_11_out, and_12_out, and_13_out, and_14_out, and_15_out, and_16_out, and_17_out, and_18_out,
       and_19_out, and_20_out, and_21_out, and_22_out, and_23_out, not_1_out, not_2_out, not_3_out,
       not_4_out, not_5_out, not_6_out, not_7_out, not_8_out, not_9_out, not_10_out, not_11_out, not_12_out,
       not_13_out, not_14_out, not_15_out, not_16_out, not_17_out, not_18_out, not_19_out, not_20_out,
       not_21_out, not_22_out, not_23_out, not_24_out, not_25_out, not_26_out, not_27_out, not_28_out,
       not_29_out, not_30_out, not_31_out, not_32_out, not_33_out, not_34_out, not_35_out, not_36_out,
       not_37_out, not_38_out, not_39_out, not_40_out, not_41_out, not_42_out, not_43_out, not_44_out,
       not_45_out, not_46_out, not_47_out, not_48_out, not_49_out, not_50_out, not_51_out, not_52_out,
       not_53_out, not_54_out, not_55_out, not_56_out, not_57_out, not_58_out, not_59_out, not_60_out,
       not_61_out, not_62_out, not_63_out, not_64_out, not_65_out, not_66_out, not_67_out, not_68_out,
       not_69_out, not_70_out, not_71_out, not_72_out, not_73_out, not_74_out, not_75_out, not_76_out,
       not_77_out, not_78_out, not_79_out, not_80_out, not_81_out, not_82_out, not_83_out, not_84_out,
       not_85_out, not_86_out, not_87_out, not_88_out, not_89_out, not_90_out, not_91_out, not_92_out,
       not_93_out, not_94_out, not_95_out, not_96_out, not_97_out, not_98_out, not_99_out, not_100_out,
       not_101_out, not_102_out, not_103_out, not_104_out, not_105_out, not_106_out, not_107_out,
       not_108_out, not_109_out, not_110_out, not_111_out, not_112_out, not_113_out, not_114_out,
       not_115_out, not_116_out, not_117_out, not_118_out, not_119_out, not_120_out, not_121_out,
       not_122_out, not_123_out, not_124_out, not_125_out, not_126_out, not_127_out, not_128_out,
       not_129_out, not_130_out, not_131_out, not_132_out, not_133_out, not_134_out, not_135_out,
       not_136_out, not_137_out, not_138_out, not_139_out, not_140_out, not_141_out, not_142_out,
       not_143_out, not_144_out, not_145_out, not_146_out, not_147_out, not_148_out, not_149_out,
       not_150_out, not_151_out, not_152_out, not_153_out, not_154_out, not_155_out, not_156_out,
       not_157_out, not_158_out, not_159_out, not_160_out, not_161_out, not_162_out, not_163_out,
       not_164_out, not_165_out, not_166_out, not_167_out, not_168_out;

  not not_1 (not_1_out, OP2);
  not not_2 (not_2_out, OP3);
  not not_3 (not_3_out, OP4);
  not not_4 (not_4_out, OP5);
  not not_5 (not_5_out, OP6);
  not not_6 (not_6_out, F12);
  not not_7 (not_7_out, F13);
  not not_8 (not_8_out, OP2);
  not not_9 (not_9_out, OP3);
  not not_10 (not_10_out, OP4);
  not not_11 (not_11_out, OP5);
  not not_12 (not_12_out, OP6);
  not not_13 (not_13_out, F12);
  not not_14 (not_14_out, F14);
  not not_15 (not_15_out, OP2);
  not not_16 (not_16_out, OP3);
  not not_17 (not_17_out, OP4);
  not not_18 (not_18_out, OP6);
  not not_19 (not_19_out, F12);
  not not_20 (not_20_out, F14);
  not not_21 (not_21_out, OP2);
  not not_22 (not_22_out, OP3);
  not not_23 (not_23_out, OP5);
  not not_24 (not_24_out, OP6);
  not not_25 (not_25_out, F12);
  not not_26 (not_26_out, F13);
  not not_27 (not_27_out, OP2);
  not not_28 (not_28_out, OP3);
  not not_29 (not_29_out, OP4);
  not not_30 (not_30_out, OP6);
  not not_31 (not_31_out, F12);
  not not_32 (not_32_out, F14);
  not not_33 (not_33_out, OP2);
  not not_34 (not_34_out, OP3);
  not not_35 (not_35_out, OP5);
  not not_36 (not_36_out, OP6);
  not not_37 (not_37_out, F12);
  not not_38 (not_38_out, OP2);
  not not_39 (not_39_out, OP3);
  not not_40 (not_40_out, OP5);
  not not_41 (not_41_out, OP6);
  not not_42 (not_42_out, F13);
  not not_43 (not_43_out, F25);
  not not_44 (not_44_out, F30);
  not not_45 (not_45_out, OP2);
  not not_46 (not_46_out, OP3);
  not not_47 (not_47_out, OP5);
  not not_48 (not_48_out, OP6);
  not not_49 (not_49_out, F25);
  not not_50 (not_50_out, OP2);
  not not_51 (not_51_out, OP3);
  not not_52 (not_52_out, OP5);
  not not_53 (not_53_out, OP6);
  not not_54 (not_54_out, OP2);
  not not_55 (not_55_out, OP3);
  not not_56 (not_56_out, OP5);
  not not_57 (not_57_out, OP6);
  not not_58 (not_58_out, F12);
  not not_59 (not_59_out, F13);
  not not_60 (not_60_out, OP2);
  not not_61 (not_61_out, OP3);
  not not_62 (not_62_out, OP5);
  not not_63 (not_63_out, OP6);
  not not_64 (not_64_out, F12);
  not not_65 (not_65_out, F14);
  not not_66 (not_66_out, OP2);
  not not_67 (not_67_out, OP3);
  not not_68 (not_68_out, OP5);
  not not_69 (not_69_out, OP6);
  not not_70 (not_70_out, F12);
  not not_71 (not_71_out, OP2);
  not not_72 (not_72_out, OP3);
  not not_73 (not_73_out, OP5);
  not not_74 (not_74_out, OP6);
  not not_75 (not_75_out, F13);
  not not_76 (not_76_out, F25);
  not not_77 (not_77_out, F30);
  not not_78 (not_78_out, OP2);
  not not_79 (not_79_out, OP3);
  not not_80 (not_80_out, OP6);
  not not_81 (not_81_out, F12);
  not not_82 (not_82_out, F13);
  not not_83 (not_83_out, F14);
  not not_84 (not_84_out, F25);
  not not_85 (not_85_out, OP2);
  not not_86 (not_86_out, OP3);
  not not_87 (not_87_out, OP6);
  not not_88 (not_88_out, F12);
  not not_89 (not_89_out, F25);
  not not_90 (not_90_out, F30);
  not not_91 (not_91_out, OP2);
  not not_92 (not_92_out, OP3);
  not not_93 (not_93_out, OP5);
  not not_94 (not_94_out, OP6);
  not not_95 (not_95_out, F25);
  not not_96 (not_96_out, OP2);
  not not_97 (not_97_out, OP3);
  not not_98 (not_98_out, OP5);
  not not_99 (not_99_out, OP6);
  not not_100 (not_100_out, OP3);
  not not_101 (not_101_out, OP6);
  not not_102 (not_102_out, F25);
  not not_103 (not_103_out, F30);
  not not_104 (not_104_out, OP2);
  not not_105 (not_105_out, OP3);
  not not_106 (not_106_out, OP2);
  not not_107 (not_107_out, OP3);
  not not_108 (not_108_out, F13);
  not not_109 (not_109_out, F14);
  not not_110 (not_110_out, OP4);
  not not_111 (not_111_out, F12);
  not not_112 (not_112_out, F13);
  not not_113 (not_113_out, F14);
  not not_114 (not_114_out, OP3);
  not not_115 (not_115_out, OP6);
  not not_116 (not_116_out, OP4);
  not not_117 (not_117_out, OP2);
  not not_118 (not_118_out, OP3);
  not not_119 (not_119_out, F12);
  not not_120 (not_120_out, F13);
  not not_121 (not_121_out, F14);
  not not_122 (not_122_out, F25);
  not not_123 (not_123_out, F30);
  not not_124 (not_124_out, OP2);
  not not_125 (not_125_out, OP3);
  not not_126 (not_126_out, OP4);
  not not_127 (not_127_out, OP6);
  not not_128 (not_128_out, F12);
  not not_129 (not_129_out, F14);
  not not_130 (not_130_out, OP2);
  not not_131 (not_131_out, OP3);
  not not_132 (not_132_out, OP4);
  not not_133 (not_133_out, F12);
  not not_134 (not_134_out, F13);
  not not_135 (not_135_out, F14);
  not not_136 (not_136_out, OP2);
  not not_137 (not_137_out, OP3);
  not not_138 (not_138_out, OP4);
  not not_139 (not_139_out, F13);
  not not_140 (not_140_out, F14);
  not not_141 (not_141_out, OP3);
  not not_142 (not_142_out, OP4);
  not not_143 (not_143_out, F12);
  not not_144 (not_144_out, F13);
  not not_145 (not_145_out, F14);
  not not_146 (not_146_out, OP4);
  not not_147 (not_147_out, OP3);
  not not_148 (not_148_out, OP6);
  not not_149 (not_149_out, OP2);
  not not_150 (not_150_out, OP3);
  not not_151 (not_151_out, OP4);
  not not_152 (not_152_out, OP5);
  not not_153 (not_153_out, OP6);
  not not_154 (not_154_out, F12);
  not not_155 (not_155_out, F13);
  not not_156 (not_156_out, OP2);
  not not_157 (not_157_out, OP3);
  not not_158 (not_158_out, OP4);
  not not_159 (not_159_out, F13);
  not not_160 (not_160_out, OP2);
  not not_161 (not_161_out, OP3);
  not not_162 (not_162_out, F12);
  not not_163 (not_163_out, OP2);
  not not_164 (not_164_out, OP3);
  not not_165 (not_165_out, OP2);
  not not_166 (not_166_out, OP3);
  not not_167 (not_167_out, F13);
  not not_168 (not_168_out, F14);
  and and_1 (and_1_out, not_1_out, not_2_out, not_3_out, not_4_out, not_5_out, not_6_out, not_7_out, F14);
  and and_2 (and_2_out, not_8_out, not_9_out, not_10_out, not_11_out, not_12_out, not_13_out, F13, not_14_out);
  and and_3 (MemWrite, not_15_out, not_16_out, not_17_out, OP5, not_18_out, not_19_out, F13, not_20_out);
  and and_4 (and_4_out, not_21_out, not_22_out, not_23_out, not_24_out, not_25_out, not_26_out, F14);
  and and_5 (and_5_out, not_27_out, not_28_out, not_29_out, not_30_out, not_31_out, F13, not_32_out);
  and and_6 (and_6_out, not_33_out, not_34_out, OP4, not_35_out, not_36_out, not_37_out);
  and and_7 (and_7_out, not_38_out, not_39_out, OP4, not_40_out, not_41_out, not_42_out, not_43_out, not_44_out);
  and and_8 (and_8_out, not_45_out, not_46_out, OP4, not_47_out, not_48_out, F14, not_49_out);
  and and_9 (and_9_out, not_50_out, not_51_out, OP4, not_52_out, not_53_out, F13, F14);
  and and_10 (and_10_out, not_54_out, not_55_out, not_56_out, not_57_out, not_58_out, not_59_out, F14);
  and and_11 (and_11_out, not_60_out, not_61_out, not_62_out, not_63_out, not_64_out, F13, not_65_out);
  and and_12 (and_12_out, not_66_out, not_67_out, OP4, not_68_out, not_69_out, not_70_out);
  and and_13 (and_13_out, not_71_out, not_72_out, OP4, not_73_out, not_74_out, not_75_out, not_76_out, not_77_out);
  and and_14 (and_14_out, not_78_out, not_79_out, OP4, not_80_out, not_81_out, not_82_out, not_83_out, not_84_out);
  and and_15 (and_15_out, not_85_out, not_86_out, OP4, not_87_out, not_88_out, not_89_out, not_90_out);
  and and_16 (and_16_out, not_91_out, not_92_out, OP4, not_93_out, not_94_out, F14, not_95_out);
  and and_17 (and_17_out, not_96_out, not_97_out, OP4, not_98_out, not_99_out, F13, F14);
  and and_18 (and_18_out, not_100_out, OP4, OP5, not_101_out, F13, not_102_out, not_103_out);
  and and_19 (and_19_out, not_104_out, not_105_out, OP4, OP5, OP6, F13, F14);
  and and_20 (and_20_out, not_106_out, not_107_out, OP4, OP5, OP6, F12, not_108_out, not_109_out);
  and and_21 (and_21_out, OP2, not_110_out, OP5, OP6, not_111_out, not_112_out, not_113_out);
  and and_22 (and_22_out, OP2, not_114_out, OP4, OP5, not_115_out);
  and and_23 (and_23_out, OP2, OP3, not_116_out, OP5, OP6);
  and and_24 (ecall, not_117_out, not_118_out, OP4, OP5, OP6, not_119_out, not_120_out, not_121_out, not_122_out, not_123_out);
  and and_25 (S_Type, not_124_out, not_125_out, not_126_out, OP5, not_127_out, not_128_out, F13, not_129_out);
  and and_26 (BEQ, not_130_out, not_131_out, not_132_out, OP5, OP6, not_133_out, not_134_out, not_135_out);
  and and_27 (BNE, not_136_out, not_137_out, not_138_out, OP5, OP6, F12, not_139_out, not_140_out);
  and and_28 (JALR, OP2, not_141_out, not_142_out, OP5, OP6, not_143_out, not_144_out, not_145_out);
  and and_29 (JAL, OP2, OP3, not_146_out, OP5, OP6);
  and and_30 (LUI, OP2, not_147_out, OP4, OP5, not_148_out);
  and and_31 (LBU, not_149_out, not_150_out, not_151_out, not_152_out, not_153_out, not_154_out, not_155_out, F14);
  and and_32 (BGE, not_156_out, not_157_out, not_158_out, OP5, OP6, F12, not_159_out, F14);
  and and_33 (CSRRSI, not_160_out, not_161_out, OP4, OP5, OP6, not_162_out, F13, F14);
  and and_34 (CSRRCI, not_163_out, not_164_out, OP4, OP5, OP6, F12, F13, F14);
  and and_35 (CSRRW, not_165_out, not_166_out, OP4, OP5, OP6, F12, not_167_out, not_168_out);
  or or_1 (MemToReg, and_1_out, and_2_out);
  or or_2 (ALU_SRC, and_4_out, and_5_out, and_6_out, and_7_out, and_8_out, and_9_out);
  or or_3 (RegWrite, and_10_out, and_11_out, and_12_out, and_13_out, and_14_out, and_15_out, and_16_out, and_17_out, and_18_out, and_19_out, and_20_out, and_21_out, and_22_out, and_23_out);
endmodule

// ALU
module ALU (
  input  [31:0] X,
  input  [31:0] Y,
  input  [3:0] AluOP,
  output out_4,
  output Equal,
  output out_6,
  output [31:0] Result,
  output [31:0] Result_2
);

  wire [0:0] comparator_2_lt;
  wire [31:0] adder_1_out, AND_out, divider_1_out, divider_1_rem, multiplier_1_cout, multiplier_1_out,
       NOR_out, OR_out, shifter_1_out, shifter_2_out, shifter_3_out, subtractor_1_out, XOR_out;

  assign AND_out = X & Y;  // AND_Gate AND, 32 bits wide
  assign OR_out = X | Y;  // OR_Gate OR, 32 bits wide
  Shifter #(.width(32), .shift("ll")) shifter_1 (.in(X), .\dist (Y[4:0]), .out(shifter_1_out));
  Shifter #(.width(32), .shift("ar")) shifter_2 (.in(X), .\dist (Y[4:0]), .out(shifter_2_out));
  Shifter #(.width(32), .shift("lr")) shifter_3 (.in(X), .\dist (Y[4:0]), .out(shifter_3_out));
  Multiplier #(.width(32)) multiplier_1 (.a(X), .b(Y), .out(multiplier_1_out), .cout(multiplier_1_cout));  // open: cin
  Divider #(.width(32)) divider_1 (.a(X), .b(Y), .out(divider_1_out), .rem(divider_1_rem));  // open: upper
  Adder #(.width(32)) adder_1 (.a(X), .b(Y), .out(adder_1_out));  // open: cin, cout
  Subtractor #(.width(32)) subtractor_1 (.a(X), .b(Y), .out(subtractor_1_out));  // open: bin, bout
  assign XOR_out = X ^ Y;  // XOR_Gate XOR, 32 bits wide
  assign NOR_out = ~(X | Y);  // NOR_Gate NOR, 32 bits wide
  Comparator #(.width(32), .mode("twosComplement")) comparator_1 (.a(X), .b(Y), .eq(Equal), .lt(out_6));  // open: gt
  Comparator #(.width(32), .mode("unsigned")) comparator_2 (.a(X), .b(Y), .lt(comparator_2_lt[0]));  // open: gt, eq
  Multiplexer #(.select(4), .width(32), .disabled("Z"), .enable("false")) multiplexer_1 (
    .in0(shifter_1_out), .in1(shifter_2_out), .in2(shifter_3_out), .in3(multiplier_1_out),
    .in4(divider_1_out), .in5(adder_1_out), .in6(subtractor_1_out), .in7(AND_out), .in8(OR_out),
    .in9(XOR_out), .in10(NOR_out), .in11({{31{1'b0}}, out_6}), .in12({{31{1'b0}}, comparator_2_lt[0]}),
    .in13({32{1'b0}}), .in14({32{1'b0}}), .in15({32{1'b0}}), .out(Result), .sel(AluOP));
  Multiplexer #(.select(4), .width(32), .disabled("Z"), .enable("false")) multiplexer_2 (
    .in0({32{1'b0}}), .in1({32{1'b0}}), .in2({32{1'b0}}), .in3(multiplier_1_cout), .in4(divider_1_rem),
    .in5({32{1'b0}}), .in6({32{1'b0}}), .in7({32{1'b0}}), .in8({32{1'b0}}), .in9({32{1'b0}}),
    .in10({32{1'b0}}), .in11({32{1'b0}}), .in12({32{1'b0}}), .in13({32{1'b0}}), .in14({32{1'b0}}),
    .in15({32{1'b0}}), .out(Result_2), .sel(AluOP));
  Multiplexer #(.select(4), .width(1), .disabled("Z"), .enable("false")) multiplexer_3 (
    .in0(1'b0), .in1(1'b0), .in2(1'b0), .in3(1'b0), .in4(1'b0), .in5(1'b0), .in6(1'b0), .in7(1'b0),
    .in8(1'b0), .in9(1'b0), .in10(1'b0), .in11(out_6), .in12(comparator_2_lt[0]), .in13(1'b0), .in14(1'b0),
    .in15(1'b0), .sel(AluOP));  // open: out
  not not_1 (out_4, out_6);

  // Other names for the same wires on the sheet: tunnel = out_6; Result2[31:0] = Result_2; S[3:0] = AluOP;
  //   tunnel_t = out_4

  // Notes on the sheet:
  //   不要改变此引脚区域内容，也不要改变ALU封装形式
  //   输入引脚
  //   输出引脚
endmodule

module Regifile (
  input  [31:0] Din,
  input  Clk,
  input  WE,
  input  [4:0] R1_num,
  input  [4:0] W_num,
  input  [4:0] R2_num,
  output [31:0] R1,
  output [31:0] R2
);

  // RegisterFile registerfile_1: pin names not known; wires that end beside it: Din, Clk, WE, W_num, R1_num, R2_num, R1, R2
endmodule

module \单周期_多级中断  (
  input  IR1,
  input  IR2,
  input  IR3,
  output RegWrite,
  output MemWrite,
  output [31:0] PC,
  output [31:0] IR,
  output [31:0] RDin,
  output [31:0] MDin,
  output [31:0] LedData
);

  wire and_1_out, and_2_out, and_3_out, and_4_out, and_5_out, and_6_out, and_7_out, and_8_out, and_9_out,
       and_10_out, and_11_out, and_12_out, Beq, Bge, Bne, CLK, com_pc, comparator_1_eq, comparator_2_eq,
       comparator_3_eq, comparator_4_eq, comparator_5_eq, csrrci, csrrsi, csrrw, d_ff_1_q, d_ff_2_q,
       d_ff_3_q, decoder_1_out0, decoder_1_out1, decoder_1_out2, decoder_2_out1, decoder_2_out2,
       decoder_2_out3, decoder_3_out1, decoder_3_out2, decoder_3_out3, Ecall, Equal, Go, halt, IE, INT,
       IR1_q, IR1_t, IR2_q, IR2_t, IR3_q, IR3_t, IRA, IRB, IRC, JAL, JALR, Lbu, Lui, not_1_out, not_2_out,
       not_3_out, not_5_out, open, or_1_out, or_2_out, or_8_out, or_9_out, or_10_out, or_13_out, or_15_out,
       or_16_out, or_17_out, or_18_out, or_19_out, pHigh, register_3_q, rst1, rst2, rst3, S, tunnel, Uret,
       W1, W2, W3, \单周期硬布线控制器_1_alu_src , \单周期硬布线控制器_1_memtoreg ;
  wire [1:0] cause0_q, cause1_q, cause2_q, counter_2_q, curCause, priority_encoder_1_out, subtractor_1_out;
  wire [3:0] \单周期硬布线控制器_1_alu_op ;
  wire [4:0] bit_extender_5_out, minus, multiplexer_6_out, multiplexer_7_out, subtractor_2_out;
  wire [11:0] multiplexer_8_out;
  wire [15:0] \总周期数 ;
  wire [31:0] adder_2_out, bit_extender_1_out, bit_extender_2_out, bit_extender_3_out, bit_extender_4_out,
       calc, INTPC, multiplexer_1_out, multiplexer_2_out, multiplexer_3_out, multiplexer_5_out,
       multiplexer_11_out, multiplexer_12_out, multiplexer_13_out, multiplexer_14_out, multiplexer_15_out,
       multiplexer_16_out, multiplexer_17_out, multiplexer_19_out, multiplexer_20_out, NEXTPC, PC_4,
       ram_1_data, RETPC, rs1_v, shifter_1_out, shifter_2_out, shifter_4_out, shifter_5_out;

  Clock #(.highDuration(1), .lowDuration(1)) clock_1 (.out(CLK));
  Button _1 ();  // open: out
  Button _2 ();  // open: out
  Button _3 ();  // open: out
  Button \u_继续运行  (.out(Go));
  LED #(.active("true")) led_1 (.in(W1));
  LED #(.active("true")) led_2 (.in(W2));
  LED #(.active("true")) led_3 (.in(W3));
  Hex_Digit_Display hex_digit_display_1 (.value(LedData[31:28]));  // open: dp
  Comparator #(.width(16), .mode("twosComplement")) comparator_1 (
    .a(\总周期数 ), .b(16'h7), .eq(comparator_1_eq));  // open: gt, lt
  Comparator #(.width(16), .mode("twosComplement")) comparator_2 (
    .a(\总周期数 ), .b(16'h241), .eq(comparator_2_eq));  // open: gt, lt
  Multiplexer #(.select(1), .width(32), .disabled("Z"), .enable("false")) multiplexer_1 (
    .in0(NEXTPC), .in1(INTPC), .out(multiplexer_1_out), .sel(INT));
  Multiplexer #(.select(1), .width(32), .disabled("Z"), .enable("false")) multiplexer_2 (
    .in0(multiplexer_1_out), .in1(RETPC), .out(multiplexer_2_out), .sel(Uret));
  not not_1 (not_1_out, Equal);
  not not_2 (not_2_out, Equal);
  Hex_Digit_Display hex_digit_display_2 (.value(LedData[27:24]));  // open: dp
  Hex_Digit_Display hex_digit_display_3 (.value(LedData[23:20]));  // open: dp
  Comparator #(.width(16), .mode("twosComplement")) comparator_3 (
    .a(16'h258), .b(\总周期数 ), .eq(comparator_3_eq));  // open: gt, lt
  or or_1 (or_1_out, comparator_3_eq, comparator_4_eq);
  Comparator #(.width(16), .mode("twosComplement")) comparator_4 (
    .a(\总周期数 ), .b(16'h1), .eq(comparator_4_eq));  // open: gt, lt
  Comparator #(.width(16), .mode("twosComplement")) comparator_5 (
    .a(\总周期数 ), .b(16'h4), .eq(comparator_5_eq));  // open: gt, lt
  or or_2 (or_2_out, comparator_1_eq, comparator_2_eq);
  or or_3 (W1, IR1_q, d_ff_1_q);
  or or_4 (W2, IR2_q, d_ff_2_q);
  or or_5 (W3, IR3_q, d_ff_3_q);
  Counter #(.width(16), .max('hffff), .ongoal("wrap"), .trigger("rising"), .behavior("old")) counter_1 (
    .count(halt), .Q(\总周期数 ), .clk(CLK));  // open: load, D, carry, clr, preset
  Register #(.width(32), .trigger("rising"), .Select("low")) u_PC (
    .D(multiplexer_2_out), .en(halt), .Q(PC), .clk(CLK));  // open: clr
  assign bit_extender_1_out = {{20{IR[31]}}, {IR[31], IR[7], IR[30:25], IR[11:8]}};  // Bit_Extender bit_extender_1
  Multiplexer #(.select(1), .width(32), .disabled("Z"), .enable("false")) multiplexer_3 (
    .in0(bit_extender_1_out), .in1(bit_extender_2_out), .out(multiplexer_3_out), .sel(JAL));
  assign bit_extender_2_out = {{12{IR[31]}}, {IR[31], IR[19:12], IR[20], IR[30:21]}};  // Bit_Extender bit_extender_2
  and and_1 (and_1_out, Beq, Equal);
  and and_2 (and_2_out, not_1_out, Bne);
  and and_3 (and_3_out, Bge, tunnel);
  not not_3 (not_3_out, and_4_out);
  and and_4 (and_4_out, Ecall, Equal);
  and and_5 (and_5_out, Ecall, not_2_out);
  Hex_Digit_Display hex_digit_display_4 (.value(LedData[19:16]));  // open: dp
  Hex_Digit_Display hex_digit_display_5 (.value(LedData[15:12]));  // open: dp
  Pull_Resistor #(.pull(0)) pull_resistor_1 (.node(IRA));
  assign IRA = or_1_out ? ~CLK : 1'bz;  // Controlled_Inverter controlled_inverter_1
  Pull_Resistor #(.pull(0)) pull_resistor_2 (.node(IRB));
  assign IRB = comparator_5_eq ? ~CLK : 1'bz;  // Controlled_Inverter controlled_inverter_2
  Pull_Resistor #(.pull(0)) pull_resistor_3 (.node(IRC));
  assign IRC = or_2_out ? ~CLK : 1'bz;  // Controlled_Inverter controlled_inverter_3
  D_Flip_Flop #(.trigger("rising"), .Pre_Clr_Positions("LEGACY"), .NegatePresetClear("false"), .enable("true"), .NewFFLayout("false")) d_ff_1 (
    .clk(IRA), .D(1'b1), .Q(d_ff_1_q), .reset(IR1_q));  // open: Qn, preset, en
  D_Flip_Flop #(.trigger("rising"), .Pre_Clr_Positions("LEGACY"), .NegatePresetClear("false"), .enable("true"), .NewFFLayout("false")) d_ff_2 (
    .clk(IRB), .D(1'b1), .Q(d_ff_2_q), .reset(IR2_q));  // open: Qn, preset, en
  D_Flip_Flop #(.trigger("rising"), .Pre_Clr_Positions("LEGACY"), .NegatePresetClear("false"), .enable("true"), .NewFFLayout("false")) d_ff_3 (
    .clk(IRC), .D(1'b1), .Q(d_ff_3_q), .reset(IR3_q));  // open: Qn, preset, en
  Adder #(.width(32)) adder_1 (.a(PC), .b(32'h4), .out(PC_4));  // open: cin, cout
  Shifter #(.width(32), .shift("ll")) shifter_1 (.in(multiplexer_3_out), .\dist (5'b00001), .out(shifter_1_out));
  or or_6 (com_pc, JAL, and_1_out, and_2_out, and_3_out);
  or or_7 (halt, Go, not_3_out);
  Register #(.width(32), .trigger("rising"), .Select("low")) register_1 (
    .D(MDin), .en(and_5_out), .Q(LedData), .clk(CLK));  // open: clr
  Hex_Digit_Display hex_digit_display_6 (.value(LedData[7:4]));  // open: dp
  Hex_Digit_Display hex_digit_display_7 (.value(LedData[11:8]));  // open: dp
  // Probe on \总周期数 
  or or_8 (or_8_out, d_ff_1_q, IR1_q);
  or or_9 (or_9_out, d_ff_2_q, IR2_q);
  or or_10 (or_10_out, d_ff_3_q, IR3_q);
  // RiscV_Probe riscv_probe_1: pin names not known; wires that end beside it: IR
  Adder #(.width(32)) adder_2 (.a(PC), .b(shifter_1_out), .out(adder_2_out));  // open: cin, cout
  Multiplexer #(.select(1), .width(32), .disabled("Z"), .enable("false")) multiplexer_4 (
    .in0(multiplexer_5_out), .in1(calc), .out(NEXTPC), .sel(JALR));
  Hex_Digit_Display hex_digit_display_8 (.value(LedData[3:0]));  // open: dp
  and and_6 (and_6_out, or_8_out, ~rst1);  // AND_Gate
  and and_7 (and_7_out, or_9_out, ~rst2);  // AND_Gate
  and and_8 (and_8_out, or_10_out, ~rst3);  // AND_Gate
  ROM #(.addrWidth(10), .dataWidth(32), .Select("high")) rom_1 (.addr(PC[11:2]), .data(IR));
  Multiplexer #(.select(1), .width(32), .disabled("Z"), .enable("false")) multiplexer_5 (
    .in0(PC_4), .in1(adder_2_out), .out(multiplexer_5_out), .sel(com_pc));
  D_Flip_Flop #(.trigger("rising"), .Pre_Clr_Positions("LEGACY"), .NegatePresetClear("false"), .enable("true"), .NewFFLayout("false")) u_IR1 (
    .clk(CLK), .D(and_6_out), .Q(IR1_q));  // open: Qn, preset, en, reset
  D_Flip_Flop #(.trigger("rising"), .Pre_Clr_Positions("LEGACY"), .NegatePresetClear("false"), .enable("true"), .NewFFLayout("false")) u_IR2 (
    .clk(CLK), .D(and_7_out), .Q(IR2_q));  // open: Qn, preset, en, reset
  D_Flip_Flop #(.trigger("rising"), .Pre_Clr_Positions("LEGACY"), .NegatePresetClear("false"), .enable("true"), .NewFFLayout("false")) u_IR3 (
    .clk(CLK), .D(and_8_out), .Q(IR3_q));  // open: Qn, preset, en, reset
  or or_11 (IR1_t, IR1, IRA);
  \单周期硬布线控制器  \u_单周期硬布线控制器_1  (
    .Funct({IR[30], IR[25], IR[14:12]}), .OP(IR[6:2]), .ALU_OP(\单周期硬布线控制器_1_alu_op ),
    .MemToReg(\单周期硬布线控制器_1_memtoreg ), .MemWrite(MemWrite), .ALU_SRC(\单周期硬布线控制器_1_alu_src ),
    .RegWrite(RegWrite), .ecall(Ecall), .S_type(S), .Jalr(JALR), .Beq(Beq), .JAL(JAL), .Bne(Bne), .Lui(Lui),
    .Lbu(Lbu), .Bge(Bge), .uret(Uret), .IR21(IR[21]), .csrrsi(csrrsi), .csrrci(csrrci), .csrrw(csrrw));
  Multiplexer #(.select(1), .width(5), .disabled("Z"), .enable("false")) multiplexer_6 (
    .in0(IR[19:15]), .in1(5'b10001), .out(multiplexer_6_out), .sel(Ecall));
  Comparator #(.width(12), .mode("twosComplement")) comparator_6 (.a(IR[31:20]), .b(12'h4), .eq(open));  // open: gt, lt
  assign bit_extender_3_out = {{12{IR[31]}}, IR[31:12]};  // Bit_Extender bit_extender_3
  or or_12 (IR2_t, IR2, IRB);
  or or_13 (or_13_out, INT, Uret);
  Priority_Encoder #(.select(2), .disabled("Z")) priority_encoder_1 (
    .in0(1'b1), .in1(IR1_q), .in2(IR2_q), .in3(IR3_q), .out(priority_encoder_1_out));  // open: gs, en_out, en_in
  and and_9 (and_9_out, pHigh, IE);
  Multiplexer #(.select(1), .width(5), .disabled("Z"), .enable("false")) multiplexer_7 (
    .in0(IR[24:20]), .in1(5'b01010), .out(multiplexer_7_out), .sel(Ecall));
  Multiplexer #(.select(1), .width(12), .disabled("Z"), .enable("false")) multiplexer_8 (
    .in0(IR[31:20]), .in1({IR[31:25], IR[11:7]}), .out(multiplexer_8_out), .sel(S));
  Multiplexer #(.select(1), .width(32), .disabled("Z"), .enable("false")) multiplexer_9 (
    .in0(multiplexer_11_out), .in1(32'h1), .out(RDin), .sel(csrrci));
  Shifter #(.width(32), .shift("ll")) shifter_2 (.in(bit_extender_3_out), .\dist (5'b01100), .out(shifter_2_out));
  Decoder #(.select(2), .tristate("false"), .disabled("Z"), .enable("false")) decoder_1 (
    .out0(decoder_1_out0), .out1(decoder_1_out1), .out2(decoder_1_out2), .sel(counter_2_q));  // open: out3
  Counter #(.width(2), .max('h3), .ongoal("wrap"), .trigger("rising"), .behavior("new")) counter_2 (
    .count(or_13_out), .Q(counter_2_q), .clk(CLK), .down(Uret));  // open: load, D, carry, clr, preset
  Multiplexer #(.select(2), .width(32), .disabled("Z"), .enable("false")) multiplexer_10 (
    .in1(32'h30ac), .in2(32'h3170), .in3(32'h3234), .out(INTPC), .sel(priority_encoder_1_out));  // open: in0
  Register #(.width(1), .trigger("falling"), .Select("low")) register_2 (
    .D(and_9_out), .Q(INT), .clk(CLK));  // open: en, clr
  Regifile regifile_1 (
    .Din(RDin), .Clk(CLK), .R1(rs1_v), .R2(MDin), .WE(RegWrite), .W_num(IR[11:7]),
    .R1_num(multiplexer_6_out), .R2_num(multiplexer_7_out));
  assign bit_extender_4_out = {{20{multiplexer_8_out[11]}}, multiplexer_8_out};  // Bit_Extender bit_extender_4
  Multiplexer #(.select(1), .width(32), .disabled("Z"), .enable("false")) multiplexer_11 (
    .in0(multiplexer_15_out), .in1({32{1'b0}}), .out(multiplexer_11_out), .sel(and_10_out));
  and and_10 (and_10_out, csrrsi, open);
  or or_14 (IR3_t, IR3, IRC);
  Register #(.width(32), .trigger("rising"), .Select("low")) EPC (
    .D(multiplexer_12_out), .en(or_15_out), .Q(RETPC), .clk(CLK));  // open: clr
  Multiplexer #(.select(1), .width(32), .disabled("Z"), .enable("false")) multiplexer_12 (
    .in0(NEXTPC), .in1(rs1_v), .out(multiplexer_12_out), .sel(csrrw));
  or or_15 (or_15_out, INT, csrrw);
  Multiplexer #(.select(1), .width(32), .disabled("Z"), .enable("false")) multiplexer_13 (
    .in0(MDin), .in1(bit_extender_4_out), .out(multiplexer_13_out), .sel(\单周期硬布线控制器_1_alu_src ));
  or or_16 (or_16_out, and_12_out, csrrw);
  Multiplexer #(.select(1), .width(32), .disabled("Z"), .enable("false")) multiplexer_14 (
    .in0(multiplexer_17_out), .in1(shifter_2_out), .out(multiplexer_14_out), .sel(Lui));
  Multiplexer #(.select(1), .width(32), .disabled("Z"), .enable("false")) multiplexer_15 (
    .in0(multiplexer_14_out), .in1(RETPC), .out(multiplexer_15_out), .sel(or_16_out));
  Register #(.width(2), .trigger("rising"), .Select("low")) cause0 (
    .D(priority_encoder_1_out), .en(decoder_1_out0), .Q(cause0_q), .clk(CLK));  // open: clr
  Register #(.width(2), .trigger("rising"), .Select("low")) cause1 (
    .D(priority_encoder_1_out), .en(decoder_1_out1), .Q(cause1_q), .clk(CLK));  // open: clr
  Register #(.width(2), .trigger("rising"), .Select("low")) cause2 (
    .D(priority_encoder_1_out), .en(decoder_1_out2), .Q(cause2_q), .clk(CLK));  // open: clr
  or or_17 (or_17_out, Uret, and_11_out);
  and and_11 (and_11_out, csrrsi, open);
  Multiplexer #(.select(1), .width(32), .disabled("Z"), .enable("false")) multiplexer_16 (
    .in0(multiplexer_13_out), .in1(32'ha), .out(multiplexer_16_out), .sel(Ecall));
  and and_12 (and_12_out, csrrsi, ~open);  // AND_Gate
  Multiplexer #(.select(1), .width(32), .disabled("Z"), .enable("false")) multiplexer_17 (
    .in0(multiplexer_19_out), .in1(shifter_5_out), .out(multiplexer_17_out), .sel(Lbu));
  Multiplexer #(.select(2), .width(2), .disabled("Z"), .enable("false")) multiplexer_18 (
    .in0(cause0_q), .in1(cause1_q), .in2(cause2_q), .in3(2'b00), .out(curCause), .sel(subtractor_1_out));
  Subtractor #(.width(2)) subtractor_1 (.a(counter_2_q), .b(2'b01), .out(subtractor_1_out));  // open: bin, bout
  or or_18 (or_18_out, INT, csrrci);
  Register #(.width(1), .trigger("falling"), .Select("low")) register_3 (
    .D(1'b0), .en(or_17_out), .Q(register_3_q), .clk(CLK), .preset(or_18_out));  // open: clr, cs
  ALU alu_1 (
    .X(rs1_v), .Y(multiplexer_16_out), .AluOP(\单周期硬布线控制器_1_alu_op ), .Equal(Equal), .Result(calc),
    .out_4(tunnel));  // open: Result_2, out_6
  Decoder #(.select(2), .tristate("false"), .disabled("Z"), .enable("false")) decoder_2 (
    .out1(decoder_2_out1), .out2(decoder_2_out2), .out3(decoder_2_out3), .sel(curCause));  // open: out0
  Decoder #(.select(2), .tristate("false"), .disabled("Z"), .enable("false")) decoder_3 (
    .out1(decoder_3_out1), .out2(decoder_3_out2), .out3(decoder_3_out3), .sel(curCause));  // open: out0
  not not_4 (IE, register_3_q);
  Subtractor #(.width(5)) subtractor_2 (.a(5'b11000), .b(minus), .out(subtractor_2_out));  // open: bin, bout
  Comparator #(.width(2), .mode("unsigned")) comparator_7 (
    .a(curCause), .b(priority_encoder_1_out), .lt(pHigh));  // open: gt, eq
  assign bit_extender_5_out = {{3{1'b0}}, calc[1:0]};  // Bit_Extender bit_extender_5
  Shifter #(.width(5), .shift("ll")) shifter_3 (.in(bit_extender_5_out), .\dist (3'b011), .out(minus));
  not not_5 (not_5_out, MemWrite);
  Shifter #(.width(32), .shift("ll")) shifter_4 (
    .in(multiplexer_19_out), .\dist (subtractor_2_out), .out(shifter_4_out));
  Shifter #(.width(32), .shift("lr")) shifter_5 (.in(shifter_4_out), .\dist (5'b11000), .out(shifter_5_out));
  and and_13 (rst1, Uret, decoder_2_out1);
  and and_14 (rst2, Uret, decoder_2_out2);
  and and_15 (rst3, decoder_2_out3, Uret);
  and and_16 (rst1, Uret, decoder_3_out1);
  and and_17 (rst2, Uret, decoder_3_out2);
  and and_18 (rst3, decoder_3_out3, Uret);
  RAM #(.addrWidth(10), .dataWidth(32), .bus("separate"), .Select("high")) ram_1 (
    .addr(calc[11:2]), .din(MDin), .data(ram_1_data), .str(MemWrite), .clk(CLK), .ld(not_5_out));  // open: sel, clr
  Multiplexer #(.select(1), .width(32), .disabled("Z"), .enable("false")) multiplexer_19 (
    .in0(multiplexer_20_out), .in1(PC_4), .out(multiplexer_19_out), .sel(or_19_out));
  Multiplexer #(.select(1), .width(32), .disabled("Z"), .enable("false")) multiplexer_20 (
    .in0(calc), .in1(ram_1_data), .out(multiplexer_20_out), .sel(\单周期硬布线控制器_1_memtoreg ));
  or or_19 (or_19_out, JAL, JALR);

  // Other names for the same wires on the sheet: imm12_B[11:0] = {IR[31], IR[7], IR[30:25], IR[11:8]};
  //   imm20_JAL[19:0] = {IR[31], IR[19:12], IR[20], IR[30:21]}

  // Notes on the sheet:
  //   中断源
  //   中断等待指示
  //   总复位信号应将除ROM以外所有存储组件全部清零
  //   多级中断测试信号模拟器
  //   Ecall选项
  //   周期数记录
  //   计算新PC
  //   数码管输出
  //   数码管输出应该用寄存器锁存，否则显示数据只能一闪而过
  //   指令存储器
  //   Reset 
  //   Reset 
  //   Reset 
  //   指令字
  //   contents of rom_1 (hex, n*v repeats v):
  //   7d000113 100413 1f41993 41f9d993 433 c00913 800b13 140413 f47413 800293 100313 499993 89e9b3 1300533
  //   2200893 73 406282b3 fe0294e3 140413 f00f93 1f47433 1c41413 800293 100313 49d993 89e9b3 1300533
  //   2200893 73 406282b3 fe0294e3 1c45413 406b0b33 b0463 f95ff06f 2b3 fff2c293 1029293 fff2e293 500533
  //   2200893 73 f5dff06f 1112023 410113 a12023 410113 812023 410113 1312023 410113 1412023 410113 1512023
  //   410113 1612023 410113 4106b73 1612023 410113 40e073 100b13 300a13 100a93 1600433 441413 14469b3
  //   1300533 2200893 73 fe0416e3 415a0a33 fe0a10e3 40f073 ffc10113 12b03 41b1073 ffc10113 12b03 ffc10113
  //   12a83 ffc10113 12a03 ffc10113 12983 ffc10113 12403 ffc10113 12503 ffc10113 12883 200073 1112023
  //   410113 a12023 410113 812023 410113 1312023 410113 1412023 410113 1512023 410113 1612023 410113
  //   4106b73 1612023 410113 40e073 200b13 300a13 100a93 1600433 441413 14469b3 1300533 2200893 73
  //   fe0416e3 415a0a33 fe0a10e3 40f073 ffc10113 12b03 41b1073 ffc10113 12b03 ffc10113 12a83 ffc10113
  //   12a03 ffc10113 12983 ffc10113 12403 ffc10113 12503 ffc10113 12883 200073 1112023 410113 a12023
  //   410113 812023 410113 1312023 410113 1412023 410113 1512023 410113 1612023 410113 4106b73 1612023
  //   410113 40e073 300b13 300a13 100a93 1600433 441413 14469b3 1300533 2200893 73 fe0416e3 415a0a33
  //   fe0a10e3 40f073 ffc10113 12b03 41b1073 ffc10113 12b03 ffc10113 12a83 ffc10113 12a03 ffc10113 12983
  //   ffc10113 12403 ffc10113 12503 ffc10113 12883 200073
  //   rs1
  //   rs2
  //   rd
  //   imm12 I
  //   imm12 S
  //   imm20 LUI
  //   Beq
  //   Bne
  //   MemToReg
  //   MemWrite
  //   AluOP
  //   AluSrcB
  //   RegWrite
  //   LBU stores the lowest byte
  //   为方便自动评测，需要输出PC，IR，寄存器堆写如数据RDin
  //   RAM写使能MemWrite、RAM写入数据MDin等信号
  //   数据存储器
endmodule

module \封装正确性测试  (
);

  wire IR1, IR2, IR3, MemW, RegW;
  wire [31:0] IR, LED, MDin, PC, RDin;

  \单周期_多级中断  \u_单周期_多级中断_1  (
    .IR1(IR1), .IR2(IR2), .IR3(IR3), .RegWrite(RegW), .MemWrite(MemW), .PC(PC), .IR(IR), .RDin(RDin),
    .MDin(MDin), .LedData(LED));

  // Notes on the sheet:
  //   请检查上面封装有无位宽不匹配，引脚标签是否和连接的标签相对应，否则无法在educoder平台上正确测试
  //   单周期+多级中断封装测试
endmodule
