// Logisim project cpu21-riscv.circ as structural Verilog: 20 circuits, main circuit ◇单周期RISC-V
module \单周期RISC_V  (
  input  IR1,
  input  IR2,
  input  IR3,
  output RegWrite,
  output MemWrite,
  output [31:0] PC,
  output [31:0] IR,
  output [31:0] RDin,
  output [31:0] MDin,
  output [31:0] LedData
);

  wire and_1_out, and_2_out, and_3_out, and_4_out, and_5_out, Beq, Bge, Bne, CLK, clock_2_out, com_pc,
       comparator_1_eq, comparator_1_lt, d_ff_1_q, Ecall, Equal, Go, halt, IR1_t, IR2_t, IR3_t, IRA, IRB,
       IRC, JAL, JALR, Lbu, Lui, nand_1_out, not_1_out, not_2_out, not_3_out, not_4_out, or_5_out, S, tunnel,
       W1, W2, W3, \单周期硬布线控制器_1_alu_src , \单周期硬布线控制器_1_memtoreg ;
  wire [3:0] \单周期硬布线控制器_1_alu_op ;
  wire [4:0] multiplexer_4_out, multiplexer_5_out;
  wire [11:0] multiplexer_6_out;
  wire [12:0] CNT_num;
  wire [15:0] \总周期数 ;
  wire [31:0] adder_2_out, alu_1_result, bit_extender_1_out, bit_extender_2_out, bit_extender_3_out,
       bit_extender_4_out, calc, multiplexer_1_out, multiplexer_2_out, multiplexer_3_out, multiplexer_7_out,
       multiplexer_9_out, multiplexer_10_out, multiplexer_11_out, PC_4, ram_1_data, regifile_1_r1,
       shifter_1_out, shifter_2_out, shifter_3_out, shifter_4_out;

  Clock #(.highDuration(1), .lowDuration(1)) clock_1 ();  // open: out
  Button _1 (.out(IRA));
  Button _2 (.out(IRB));
  Button _3 (.out(IRC));
  Button \u_继续运行  (.out(Go));
  LED #(.active("true")) led_1 (.in(W1));
  LED #(.active("true")) led_2 (.in(W2));
  LED #(.active("true")) led_3 (.in(W3));
  Hex_Digit_Display hex_digit_display_1 (.value(LedData[31:28]));  // open: dp
  Counter #(.width(16), .max('hffff), .ongoal("wrap"), .trigger("rising"), .behavior("old")) counter_1 (
    .count(halt), .Q(\总周期数 ), .clk(CLK));  // open: load, D, carry, clr, preset
  Register #(.width(32), .trigger("rising"), .Select("low")) u_PC (
    .D(multiplexer_2_out), .en(halt), .Q(PC), .clk(CLK));  // open: clr
  assign bit_extender_1_out = {{20{IR[31]}}, {IR[31], IR[7], IR[30:25], IR[11:8]}};  // Bit_Extender bit_extender_1
  Multiplexer #(.select(1), .width(32), .disabled("Z"), .enable("false")) multiplexer_1 (
    .in0(bit_extender_1_out), .in1(bit_extender_2_out), .out(multiplexer_1_out), .sel(JAL));
  assign bit_extender_2_out = {{12{IR[31]}}, {IR[31], IR[19:12], IR[20], IR[30:21]}};  // Bit_Extender bit_extender_2
  and and_1 (and_1_out, Beq, Equal);
  not not_1 (not_1_out, Equal);
  and and_2 (and_2_out, not_1_out, Bne);
  and and_3 (and_3_out, Bge, tunnel);
  Hex_Digit_Display hex_digit_display_2 (.value(LedData[27:24]));  // open: dp
  Hex_Digit_Display hex_digit_display_3 (.value(LedData[23:20]));  // open: dp
  Adder #(.width(32)) adder_1 (.a(PC), .b(32'h4), .out(PC_4));  // open: cin, cout
  Shifter #(.width(32), .shift("ll")) shifter_1 (.in(multiplexer_1_out), .\dist (5'b00001), .out(shifter_1_out));
  or or_1 (com_pc, JAL, and_1_out, and_2_out, and_3_out);
  Hex_Digit_Display hex_digit_display_4 (.value(LedData[15:12]));  // open: dp
  Hex_Digit_Display hex_digit_display_5 (.value(LedData[19:16]));  // open: dp
  // RiscV_Probe riscv_probe_1: pin names not known; wires that end beside it: IR
  Adder #(.width(32)) adder_2 (.a(PC), .b(shifter_1_out), .out(adder_2_out));  // open: cin, cout
  Multiplexer #(.select(1), .width(32), .disabled("Z"), .enable("false")) multiplexer_2 (
    .in0(multiplexer_3_out), .in1(calc), .out(multiplexer_2_out), .sel(JALR));
  Hex_Digit_Display hex_digit_display_6 (.value(LedData[11:8]));  // open: dp
  Hex_Digit_Display hex_digit_display_7 (.value(LedData[7:4]));  // open: dp
  // Probe on \总周期数 
  ROM #(.addrWidth(10), .dataWidth(32), .Select("high")) rom_1 (.addr(PC[11:2]), .data(IR));
  Multiplexer #(.select(1), .width(32), .disabled("Z"), .enable("false")) multiplexer_3 (
    .in0(PC_4), .in1(adder_2_out), .out(multiplexer_3_out), .sel(com_pc));
  Hex_Digit_Display hex_digit_display_8 (.value(LedData[3:0]));  // open: dp
  \单周期硬布线控制器  \u_单周期硬布线控制器_1  (
    .Funct({IR[30], IR[25], IR[14:12]}), .OP(IR[6:2]), .ALU_OP(\单周期硬布线控制器_1_alu_op ),
    .MemToReg(\单周期硬布线控制器_1_memtoreg ), .MemWrite(MemWrite), .ALU_SRC(\单周期硬布线控制器_1_alu_src ),
    .RegWrite(RegWrite), .ecall(Ecall), .S_type(S), .Jalr(JALR), .Beq(Beq), .JAL(JAL), .Bne(Bne), .Lui(Lui),
    .Lbu(Lbu), .Bge(Bge));
  assign bit_extender_3_out = {{12{IR[31]}}, IR[31:12]};  // Bit_Extender bit_extender_3
  or or_2 (IR1_t, IR1, IRA);
  Multiplexer #(.select(1), .width(5), .disabled("Z"), .enable("false")) multiplexer_4 (
    .in0(IR[19:15]), .in1(5'b10001), .out(multiplexer_4_out), .sel(Ecall));
  Multiplexer #(.select(1), .width(5), .disabled("Z"), .enable("false")) multiplexer_5 (
    .in0(IR[24:20]), .in1(5'b01010), .out(multiplexer_5_out), .sel(Ecall));
  Shifter #(.width(32), .shift("ll")) shifter_2 (.in(bit_extender_3_out), .\dist (5'b01100), .out(shifter_2_out));
  or or_3 (IR2_t, IR2, IRB);
  Regifile regifile_1 (
    .Din(RDin), .Clk(CLK), .R1(regifile_1_r1), .R2(MDin), .WE(RegWrite), .W_num(IR[11:7]),
    .R1_num(multiplexer_4_out), .R2_num(multiplexer_5_out));
  assign bit_extender_4_out = {{20{multiplexer_6_out[11]}}, multiplexer_6_out};  // Bit_Extender bit_extender_4
  Multiplexer #(.select(1), .width(12), .disabled("Z"), .enable("false")) multiplexer_6 (
    .in0(IR[31:20]), .in1({IR[31:25], IR[11:7]}), .out(multiplexer_6_out), .sel(S));
  Multiplexer #(.select(1), .width(32), .disabled("Z"), .enable("false")) multiplexer_7 (
    .in0(multiplexer_11_out), .in1(shifter_4_out), .out(multiplexer_7_out), .sel(Lbu));
  Multiplexer #(.select(1), .width(32), .disabled("Z"), .enable("false")) multiplexer_8 (
    .in0(multiplexer_7_out), .in1(shifter_2_out), .out(RDin), .sel(Lui));
  Multiplexer #(.select(1), .width(32), .disabled("Z"), .enable("false")) multiplexer_9 (
    .in0(MDin), .in1(bit_extender_4_out), .out(multiplexer_9_out), .sel(\单周期硬布线控制器_1_alu_src ));
  or or_4 (IR3_t, IR3, IRC);
  Multiplexer #(.select(1), .width(32), .disabled("Z"), .enable("false")) multiplexer_10 (
    .in0(multiplexer_9_out), .in1(32'ha), .out(multiplexer_10_out), .sel(Ecall));
  Multiplexer #(.select(1), .width(32), .disabled("Z"), .enable("false")) multiplexer_11 (
    .in0(calc), .in1(PC_4), .out(multiplexer_11_out), .sel(or_5_out));
  Shifter #(.width(32), .shift("ll")) shifter_3 (.in(multiplexer_11_out), .\dist (5'b11000), .out(shifter_3_out));
  Shifter #(.width(32), .shift("lr")) shifter_4 (.in(shifter_3_out), .\dist (5'b11000), .out(shifter_4_out));
  ALU alu_1 (
    .X(regifile_1_r1), .Y(multiplexer_10_out), .AluOP(\单周期硬布线控制器_1_alu_op ), .Equal(Equal),
    .Result(alu_1_result), .out_4(tunnel));  // open: Result_2, out_6
  or or_5 (or_5_out, JAL, JALR);
  not not_2 (not_2_out, Equal);
  not not_3 (not_3_out, MemWrite);
  not not_4 (not_4_out, and_4_out);
  and and_4 (and_4_out, Ecall, Equal);
  and and_5 (and_5_out, Ecall, not_2_out);
  RAM #(.addrWidth(10), .dataWidth(32), .bus("separate"), .Select("high")) ram_1 (
    .addr(alu_1_result[11:2]), .din(MDin), .data(ram_1_data), .str(MemWrite), .clk(CLK), .ld(not_3_out));  // open: sel, clr
  or or_6 (halt, Go, not_4_out);
  Register #(.width(32), .trigger("rising"), .Select("low")) register_1 (
    .D(MDin), .en(and_5_out), .Q(LedData), .clk(CLK));  // open: clr
  Multiplexer #(.select(1), .width(32), .disabled("Z"), .enable("false")) multiplexer_12 (
    .in0(alu_1_result), .in1(ram_1_data), .out(calc), .sel(\单周期硬布线控制器_1_memtoreg ));
  D_Flip_Flop #(.trigger("high"), .Pre_Clr_Positions("LEGACY"), .NegatePresetClear("false"), .enable("true"), .NewFFLayout("false")) d_ff_1 (.Q(d_ff_1_q));  // open: clk, D, Qn, preset, en, reset
  // Probe on 13'hc
  Comparator #(.width(13), .mode("twosComplement")) comparator_1 (
    .a(CNT_num), .b(13'hc), .eq(comparator_1_eq), .lt(comparator_1_lt));  // open: gt
  Clock #(.highDuration(1), .lowDuration(1)) clock_2 (.out(clock_2_out));
  Counter #(.width(13), .max('h1fff), .ongoal("stay"), .trigger("rising"), .behavior("old")) counter_2 (
    .count(comparator_1_lt), .Q(CNT_num), .clk(clock_2_out));  // open: load, D, carry, clr, preset
  nand nand_1 (nand_1_out, d_ff_1_q, comparator_1_eq);
  assign CLK = nand_1_out ? clock_2_out : 1'bz;  // Controlled_Buffer controlled_buffer_1
  Pull_Resistor #(.pull(1)) pull_resistor_1 (.node(CLK));

  // Other names for the same wires on the sheet: imm12_B[11:0] = {IR[31], IR[7], IR[30:25], IR[11:8]};
  //   imm20_JAL[19:0] = {IR[31], IR[19:12], IR[20], IR[30:21]}

  // Notes on the sheet:
  //   中断源
  //   中断等待指示
  //   总复位信号应将除ROM以外所有存储组件全部清零
  //   周期数记录
  //   计算新PC
  //   数码管输出
  //   指令存储器
  //   数码管输出应该用寄存器锁存，否则显示数据只能一闪而过
  //   指令字
  //   contents of rom_1 (hex, n*v repeats v):
  //   100493 100006f 100493 200913 300993 100006f 100493 200913 300993 100006f 100493 200913 300993
  //   100006f 100493 200913 300993 29c000ef 100413 100493 1f49493 900533 2200893 73 24d493 48463 fedff06f
  //   900533 2200893 73 100493 249493 900533 2200893 73 48463 fedff06f 100493 1f49493 900533 2200893 73
  //   4034d493 900533 2200893 73 4044d493 900533 2200893 73 4044d493 900533 2200893 73 4044d493 900533
  //   2200893 73 4044d493 900533 2200893 73 4044d493 900533 2200893 73 4044d493 900533 2200893 73 4044d493
  //   900533 2200893 73 100413 1f41993 41f9d993 433 c00913 300b13 140413 f47413 800293 100313 499993
  //   89e9b3 1300533 2200893 73 406282b3 fe0294e3 140413 f00f93 1f47433 1c41413 800293 100313 49d993
  //   89e9b3 1300533 2200893 73 406282b3 fe0294e3 1c45413 406b0b33 b0463 f95ff06f 2b3 fff2c293 829293
  //   ff2e293 500533 2200893 73 fff00413 493 84a023 140413 448493 84a023 140413 448493 84a023 140413
  //   448493 84a023 140413 448493 84a023 140413 448493 84a023 140413 448493 84a023 140413 448493 84a023
  //   140413 448493 84a023 140413 448493 84a023 140413 448493 84a023 140413 448493 84a023 140413 448493
  //   84a023 140413 448493 84a023 140413 448493 84a023 140413 448493 84a023 140413 448493 140413 433
  //   3c00493 42983 4aa03 149a2b3 28663 134a023 1442023 ffc48493 fe9412e3 800533 2200893 73 440413 3c00493
  //   fc9416e3 a00893 73 413 140413 800533 2200893 73 240413 800533 2200893 73 340413 800533 2200893 73
  //   440413 800533 2200893 73 540413 800533 2200893 73 640413 800533 2200893 73 740413 800533 2200893 73
  //   840413 800533 2200893 2200893 73 8067
  //   rs1
  //   rs2
  //   rd
  //   imm20 LUI
  //   Beq
  //   Bne
  //   MemToReg
  //   MemWrite
  //   AluOP
  //   AluSrcB
  //   RegWrite
  //   imm12 I
  //   imm12 S
  //   LBU stores the lowest byte
  //   Ecall选项
  //   为方便自动评测，需要输出PC，IR，寄存器堆写如数据RDin
  //   数据存储器
  //   RAM写使能MemWrite、RAM写入数据MDin等信号
  //   控制位
  //   暂停节拍，不能为0
  //   戳工具置1进入计数暂停模式，ctrl+k时钟自动运行到对应节拍暂停
  //   ctrl+k关闭时钟连续运行，将控制位置零，进入单步调试模式调试
  //   用这个时钟源需要去掉电路中的其他时钟源
  //   可计数暂停的时钟源
endmodule

// 单周期硬布线控制器
module \单周期硬布线控制器  (
  input  [4:0] OP,
  input  [4:0] Funct,
  output [3:0] ALU_OP,
  output MemToReg,
  output MemWrite,
  output ALU_SRC,
  output RegWrite,
  output ecall,
  output S_type,
  output Beq,
  output Bne,
  output Jalr,
  output JAL,
  output Lui,
  output Lbu,
  output Bge
);

  \运算控制器自动生成  \u_运算控制器自动生成_1  (
    .OP2(OP[0]), .OP3(OP[1]), .OP4(OP[2]), .OP5(OP[3]), .OP6(OP[4]), .F12(Funct[0]), .F13(Funct[1]),
    .F14(Funct[2]), .F25(Funct[3]), .F30(Funct[4]), .S0(ALU_OP[0]), .S1(ALU_OP[1]), .S2(ALU_OP[2]),
    .S3(ALU_OP[3]));
  \控制信号自动生成  \u_控制信号自动生成_1  (
    .OP2(OP[0]), .OP3(OP[1]), .OP4(OP[2]), .OP5(OP[3]), .OP6(OP[4]), .MemToReg(MemToReg), .F12(Funct[0]),
    .F13(Funct[1]), .F14(Funct[2]), .F25(Funct[3]), .F30(Funct[4]), .MemWrite(MemWrite), .ALU_SRC(ALU_SRC),
    .RegWrite(RegWrite), .ecall(ecall), .S_Type(S_type), .BEQ(Beq), .BNE(Bne), .JALR(Jalr), .JAL(JAL),
    .LUI(Lui), .LBU(Lbu), .BGE(Bge));

  // Other names for the same wires on the sheet: OP_CODE[4:0] = OP

  // Notes on the sheet:
  //   运算器控制器，根据指令生成运算器功能选择信号
  //   控制信号生成，产生数据通路需要的其他控制信号
endmodule

// 运算器控制器
module \运算控制器自动生成  (
  input  OP2,
  input  OP3,
  input  OP4,
  input  OP5,
  input  OP6,
  input  F12,
  input  F13,
  input  F14,
  input  F25,
  input  F30,
  output S0,
  output S1,
  output S2,
  output S3
);

  wire and_1_out, and_2_out, and_3_out, and_4_out, and_5_out, and_6_out, and_7_out, and_8_out, and_9_out,
       and_10_out, and_11_out, and_12_out, and_13_out, and_14_out, and_15_out, and_16_out, and_17_out,
       and_18_out, and_19_out, and_20_out, and_21_out, and_22_out, and_23_out, not_1_out, not_2_out,
       not_3_out, not_4_out, not_5_out, not_6_out, not_7_out, not_8_out, not_9_out, not_10_out, not_11_out,
       not_12_out, not_13_out, not_14_out, not_15_out, not_16_out, not_17_out, not_18_out, not_19_out,
       not_20_out, not_21_out, not_22_out, not_23_out, not_24_out, not_25_out, not_26_out, not_27_out,
       not_28_out, not_29_out, not_30_out, not_31_out, not_32_out, not_33_out, not_34_out, not_35_out,
       not_36_out, not_37_out, not_38_out, not_39_out, not_40_out, not_41_out, not_42_out, not_43_out,
       not_44_out, not_45_out, not_46_out, not_47_out, not_48_out, not_49_out, not_50_out, not_51_out,
       not_52_out, not_53_out, not_54_out, not_55_out, not_56_out, not_57_out, not_58_out, not_59_out,
       not_60_out, not_61_out, not_62_out, not_63_out, not_64_out, not_65_out, not_66_out, not_67_out,
       not_68_out, not_69_out, not_70_out, not_71_out, not_72_out, not_73_out, not_74_out, not_75_out,
       not_76_out, not_77_out, not_78_out, not_79_out, not_80_out, not_81_out, not_82_out, not_83_out,
       not_84_out, not_85_out, not_86_out, not_87_out, not_88_out, not_89_out, not_90_out, not_91_out,
       not_92_out, not_93_out, not_94_out, not_95_out, not_96_out, not_97_out, not_98_out, not_99_out,
       not_100_out, not_101_out, not_102_out, not_103_out, not_104_out, not_105_out, not_106_out,
       not_107_out, not_108_out, not_109_out, not_110_out, not_111_out, not_112_out, not_113_out,
       not_114_out, not_115_out, not_116_out, not_117_out, not_118_out, not_119_out, not_120_out,
       not_121_out, not_122_out, not_123_out, not_124_out, not_125_out, not_126_out, not_127_out,
       not_128_out, not_129_out, not_130_out, not_131_out, not_132_out, not_133_out;

  not not_1 (not_1_out, OP2);
  not not_2 (not_2_out, OP3);
  not not_3 (not_3_out, OP4);
  not not_4 (not_4_out, OP6);
  not not_5 (not_5_out, F12);
  not not_6 (not_6_out, F14);
  not not_7 (not_7_out, OP2);
  not not_8 (not_8_out, OP3);
  not not_9 (not_9_out, OP5);
  not not_10 (not_10_out, OP6);
  not not_11 (not_11_out, F12);
  not not_12 (not_12_out, F13);
  not not_13 (not_13_out, OP2);
  not not_14 (not_14_out, OP3);
  not not_15 (not_15_out, OP5);
  not not_16 (not_16_out, OP6);
  not not_17 (not_17_out, F12);
  not not_18 (not_18_out, F14);
  not not_19 (not_19_out, OP2);
  not not_20 (not_20_out, OP3);
  not not_21 (not_21_out, OP6);
  not not_22 (not_22_out, F12);
  not not_23 (not_23_out, F13);
  not not_24 (not_24_out, F25);
  not not_25 (not_25_out, F30);
  not not_26 (not_26_out, OP2);
  not not_27 (not_27_out, OP3);
  not not_28 (not_28_out, OP6);
  not not_29 (not_29_out, F12);
  not not_30 (not_30_out, F14);
  not not_31 (not_31_out, F25);
  not not_32 (not_32_out, F30);
  not not_33 (not_33_out, OP2);
  not not_34 (not_34_out, OP3);
  not not_35 (not_35_out, OP5);
  not not_36 (not_36_out, OP6);
  not not_37 (not_37_out, F13);
  not not_38 (not_38_out, F25);
  not not_39 (not_39_out, OP2);
  not not_40 (not_40_out, OP3);
  not not_41 (not_41_out, OP5);
  not not_42 (not_42_out, OP6);
  not not_43 (not_43_out, OP2);
  not not_44 (not_44_out, OP3);
  not not_45 (not_45_out, OP6);
  not not_46 (not_46_out, F25);
  not not_47 (not_47_out, F30);
  not not_48 (not_48_out, OP2);
  not not_49 (not_49_out, OP3);
  not not_50 (not_50_out, OP5);
  not not_51 (not_51_out, OP6);
  not not_52 (not_52_out, F12);
  not not_53 (not_53_out, F14);
  not not_54 (not_54_out, OP2);
  not not_55 (not_55_out, OP3);
  not not_56 (not_56_out, OP6);
  not not_57 (not_57_out, F12);
  not not_58 (not_58_out, F14);
  not not_59 (not_59_out, F25);
  not not_60 (not_60_out, F30);
  not not_61 (not_61_out, OP2);
  not not_62 (not_62_out, OP3);
  not not_63 (not_63_out, OP5);
  not not_64 (not_64_out, OP6);
  not not_65 (not_65_out, F25);
  not not_66 (not_66_out, F30);
  not not_67 (not_67_out, OP2);
  not not_68 (not_68_out, OP3);
  not not_69 (not_69_out, OP5);
  not not_70 (not_70_out, OP6);
  not not_71 (not_71_out, OP2);
  not not_72 (not_72_out, OP3);
  not not_73 (not_73_out, OP6);
  not not_74 (not_74_out, F25);
  not not_75 (not_75_out, F30);
  not not_76 (not_76_out, OP2);
  not not_77 (not_77_out, OP3);
  not not_78 (not_78_out, OP6);
  not not_79 (not_79_out, F12);
  not not_80 (not_80_out, F13);
  not not_81 (not_81_out, F14);
  not not_82 (not_82_out, F25);
  not not_83 (not_83_out, OP2);
  not not_84 (not_84_out, OP3);
  not not_85 (not_85_out, OP4);
  not not_86 (not_86_out, OP6);
  not not_87 (not_87_out, F12);
  not not_88 (not_88_out, F14);
  not not_89 (not_89_out, OP2);
  not not_90 (not_90_out, OP3);
  not not_91 (not_91_out, OP5);
  not not_92 (not_92_out, OP6);
  not not_93 (not_93_out, F12);
  not not_94 (not_94_out, F13);
  not not_95 (not_95_out, F14);
  not not_96 (not_96_out, OP2);
  not not_97 (not_97_out, OP3);
  not not_98 (not_98_out, OP6);
  not not_99 (not_99_out, F12);
  not not_100 (not_100_out, F13);
  not not_101 (not_101_out, F14);
  not not_102 (not_102_out, F25);
  not not_103 (not_103_out, OP2);
  not not_104 (not_104_out, OP3);
  not not_105 (not_105_out, OP5);
  not not_106 (not_106_out, OP6);
  not not_107 (not_107_out, OP2);
  not not_108 (not_108_out, OP3);
  not not_109 (not_109_out, OP6);
  not not_110 (not_110_out, F25);
  not not_111 (not_111_out, F30);
  not not_112 (not_112_out, OP2);
  not not_113 (not_113_out, OP3);
  not not_114 (not_114_out, OP5);
  not not_115 (not_115_out, OP6);
  not not_116 (not_116_out, F12);
  not not_117 (not_117_out, OP2);
  not not_118 (not_118_out, OP3);
  not not_119 (not_119_out, OP6);
  not not_120 (not_120_out, F12);
  not not_121 (not_121_out, F25);
  not not_122 (not_122_out, F30);
  not not_123 (not_123_out, OP2);
  not not_124 (not_124_out, OP3);
  not not_125 (not_125_out, OP5);
  not not_126 (not_126_out, OP6);
  not not_127 (not_127_out, F12);
  not not_128 (not_128_out, OP2);
  not not_129 (not_129_out, OP3);
  not not_130 (not_130_out, OP6);
  not not_131 (not_131_out, F14);
  not not_132 (not_132_out, F25);
  not not_133 (not_133_out, F30);
  and and_1 (and_1_out, not_1_out, not_2_out, not_3_out, not_4_out, not_5_out, F13, not_6_out);
  and and_2 (and_2_out, not_7_out, not_8_out, OP4, not_9_out, not_10_out, not_11_out, not_12_out);
  and and_3 (and_3_out, not_13_out, not_14_out, OP4, not_15_out, not_16_out, not_17_out, not_18_out);
  and and_4 (and_4_out, not_19_out, not_20_out, OP4, not_21_out, not_22_out, not_23_out, not_24_out, not_25_out);
  and and_5 (and_5_out, not_26_out, not_27_out, OP4, not_28_out, not_29_out, not_30_out, not_31_out, not_32_out);
  and and_6 (and_6_out, not_33_out, not_34_out, OP4, not_35_out, not_36_out, not_37_out, F14, not_38_out, F30);
  and and_7 (and_7_out, not_39_out, not_40_out, OP4, not_41_out, not_42_out, F12, F13, F14);
  and and_8 (and_8_out, not_43_out, not_44_out, OP4, not_45_out, F12, F13, F14, not_46_out, not_47_out);
  and and_9 (and_9_out, not_48_out, not_49_out, OP4, not_50_out, not_51_out, not_52_out, F13, not_53_out);
  and and_10 (and_10_out, not_54_out, not_55_out, OP4, not_56_out, not_57_out, F13, not_58_out, not_59_out, not_60_out);
  and and_11 (and_11_out, not_61_out, not_62_out, OP4, not_63_out, not_64_out, F12, F14, not_65_out, not_66_out);
  and and_12 (and_12_out, not_67_out, not_68_out, OP4, not_69_out, not_70_out, F12, F13, F14);
  and and_13 (and_13_out, not_71_out, not_72_out, OP4, not_73_out, F12, F13, F14, not_74_out, not_75_out);
  and and_14 (and_14_out, not_76_out, not_77_out, OP4, OP5, not_78_out, not_79_out, not_80_out, not_81_out, not_82_out, F30);
  and and_15 (and_15_out, not_83_out, not_84_out, not_85_out, not_86_out, not_87_out, F13, not_88_out);
  and and_16 (and_16_out, not_89_out, not_90_out, OP4, not_91_out, not_92_out, not_93_out, not_94_out, not_95_out);
  and and_17 (and_17_out, not_96_out, not_97_out, OP4, not_98_out, not_99_out, not_100_out, not_101_out, not_102_out);
  and and_18 (and_18_out, not_103_out, not_104_out, OP4, not_105_out, not_106_out, F12, F13, F14);
  and and_19 (and_19_out, not_107_out, not_108_out, OP4, OP5, not_109_out, F12, F13, not_110_out, not_111_out);
  and and_20 (and_20_out, not_112_out, not_113_out, OP4, not_114_out, not_115_out, not_116_out, F14);
  and and_21 (and_21_out, not_117_out, not_118_out, OP4, not_119_out, not_120_out, F14, not_121_out, not_122_out);
  and and_22 (and_22_out, not_123_out, not_124_out, OP4, not_125_out, not_126_out, not_127_out, F13);
  and and_23 (and_23_out, not_128_out, not_129_out, OP4, OP5, not_130_out, F13, not_131_out, not_132_out, not_133_out);
  or or_1 (S2, and_15_out, and_16_out, and_17_out, and_18_out, and_19_out);
  or or_2 (S3, and_20_out, and_21_out, and_22_out, and_23_out);
  or or_3 (S0, and_1_out, and_2_out, and_3_out, and_4_out, and_5_out, and_6_out, and_7_out, and_8_out);
  or or_4 (S1, and_9_out, and_10_out, and_11_out, and_12_out, and_13_out, and_14_out);
endmodule

// 控制信号生成
module \控制信号自动生成  (
  input  OP2,
  input  OP3,
  input  OP4,
  input  OP5,
  input  OP6,
  input  F12,
  input  F13,
  input  F14,
  input  F25,
  input  F30,
  output MemToReg,
  output MemWrite,
  output ALU_SRC,
  output RegWrite,
  output ecall,
  output S_Type,
  output BEQ,
  output BNE,
  output JALR,
  output JAL,
  output LUI,
  output LBU,
  output BGE
);

  wire and_1_out, and_2_out, and_4_out, and_5_out, and_6_out, and_7_out, and_8_out, and_9_out, and_10_out,
       and_11_out, and_12_out, and_13_out, and_14_out, and_15_out, and_16_out, and_17_out, and_18_out,
       and_19_out, and_20_out, and_21_out, not_1_out, not_2_out, not_3_out, not_4_out, not_5_out, not_6_out,
       not_7_out, not_8_out, not_9_out, not_10_out, not_11_out, not_12_out, not_13_out, not_14_out,
       not_15_out, not_16_out, not_17_out, not_18_out, not_19_out, not_20_out, not_21_out, not_22_out,
       not_23_out, not_24_out, not_25_out, not_26_out, not_27_out, not_28_out, not_29_out, not_30_out,
       not_31_out, not_32_out, not_33_out, not_34_out, not_35_out, not_36_out, not_37_out, not_38_out,
       not_39_out, not_40_out, not_41_out, not_42_out, not_43_out, not_44_out, not_45_out, not_46_out,
       not_47_out, not_48_out, not_49_out, not_50_out, not_51_out, not_52_out, not_53_out, not_54_out,
       not_55_out, not_56_out, not_57_out, not_58_out, not_59_out, not_60_out, not_61_out, not_62_out,
       not_63_out, not_64_out, not_65_out, not_66_out, not_67_out, not_68_out, not_69_out, not_70_out,
       not_71_out, not_72_out, not_73_out, not_74_out, not_75_out, not_76_out, not_77_out, not_78_out,
       not_79_out, not_80_out, not_81_out, not_82_out, not_83_out, not_84_out, not_85_out, not_86_out,
       not_87_out, not_88_out, not_89_out, not_90_out, not_91_out, not_92_out, not_93_out, not_94_out,
       not_95_out, not_96_out, not_97_out, not_98_out, not_99_out, not_100_out, not_101_out, not_102_out,
       not_103_out, not_104_out, not_105_out, not_106_out, not_107_out, not_108_out, not_109_out,
       not_110_out, not_111_out, not_112_out, not_113_out, not_114_out, not_115_out, not_116_out,
       not_117_out, not_118_out, not_119_out, not_120_out, not_121_out, not_122_out, not_123_out,
       not_124_out, not_125_out, not_126_out, not_127_out, not_128_out, not_129_out, not_130_out,
       not_131_out, not_132_out, not_133_out, not_134_out, not_135_out, not_136_out, not_137_out,
       not_138_out, not_139_out, not_140_out, not_141_out, not_142_out, not_143_out, not_144_out,
       not_145_out, not_146_out, not_147_out, not_148_out, not_149_out, not_150_out, not_151_out,
       not_152_out, not_153_out;

  not not_1 (not_1_out, OP2);
  not not_2 (not_2_out, OP3);
  not not_3 (not_3_out, OP4);
  not not_4 (not_4_out, OP5);
  not not_5 (not_5_out, OP6);
  not not_6 (not_6_out, F12);
  not not_7 (not_7_out, F13);
  not not_8 (not_8_out, OP2);
  not not_9 (not_9_out, OP3);
  not not_10 (not_10_out, OP4);
  not not_11 (not_11_out, OP5);
  not not_12 (not_12_out, OP6);
  not not_13 (not_13_out, F12);
  not not_14 (not_14_out, F14);
  not not_15 (not_15_out, OP2);
  not not_16 (not_16_out, OP3);
  not not_17 (not_17_out, OP4);
  not not_18 (not_18_out, OP6);
  not not_19 (not_19_out, F12);
  not not_20 (not_20_out, F14);
  not not_21 (not_21_out, OP2);
  not not_22 (not_22_out, OP3);
  not not_23 (not_23_out, OP5);
  not not_24 (not_24_out, OP6);
  not not_25 (not_25_out, F12);
  not not_26 (not_26_out, F13);
  not not_27 (not_27_out, OP2);
  not not_28 (not_28_out, OP3);
  not not_29 (not_29_out, OP4);
  not not_30 (not_30_out, OP6);
  not not_31 (not_31_out, F12);
  not not_32 (not_32_out, F14);
  not not_33 (not_33_out, OP2);
  not not_34 (not_34_out, OP3);
  not not_35 (not_35_out, OP5);
  not not_36 (not_36_out, OP6);
  not not_37 (not_37_out, F12);
  not not_38 (not_38_out, OP2);
  not not_39 (not_39_out, OP3);
  not not_40 (not_40_out, OP5);
  not not_41 (not_41_out, OP6);
  not not_42 (not_42_out, F13);
  not not_43 (not_43_out, F25);
  not not_44 (not_44_out, F30);
  not not_45 (not_45_out, OP2);
  not not_46 (not_46_out, OP3);
  not not_47 (not_47_out, OP5);
  not not_48 (not_48_out, OP6);
  not not_49 (not_49_out, F25);
  not not_50 (not_50_out, OP2);
  not not_51 (not_51_out, OP3);
  not not_52 (not_52_out, OP5);
  not not_53 (not_53_out, OP6);
  not not_54 (not_54_out, OP2);
  not not_55 (not_55_out, OP3);
  not not_56 (not_56_out, OP5);
  not not_57 (not_57_out, OP6);
  not not_58 (not_58_out, F12);
  not not_59 (not_59_out, F13);
  not not_60 (not_60_out, OP2);
  not not_61 (not_61_out, OP3);
  not not_62 (not_62_out, OP5);
  not not_63 (not_63_out, OP6);
  not not_64 (not_64_out, F12);
  not not_65 (not_65_out, F14);
  not not_66 (not_66_out, OP2);
  not not_67 (not_67_out, OP3);
  not not_68 (not_68_out, OP5);
  not not_69 (not_69_out, OP6);
  not not_70 (not_70_out, F12);
  not not_71 (not_71_out, OP2);
  not not_72 (not_72_out, OP3);
  not not_73 (not_73_out, OP5);
  not not_74 (not_74_out, OP6);
  not not_75 (not_75_out, F13);
  not not_76 (not_76_out, F25);
  not not_77 (not_77_out, F30);
  not not_78 (not_78_out, OP2);
  not not_79 (not_79_out, OP3);
  not not_80 (not_80_out, OP6);
  not not_81 (not_81_out, F12);
  not not_82 (not_82_out, F13);
  not not_83 (not_83_out, F14);
  not not_84 (not_84_out, F25);
  not not_85 (not_85_out, OP2);
  not not_86 (not_86_out, OP3);
  not not_87 (not_87_out, OP6);
  not not_88 (not_88_out, F12);
  not not_89 (not_89_out, F25);
  not not_90 (not_90_out, F30);
  not not_91 (not_91_out, OP2);
  not not_92 (not_92_out, OP3);
  not not_93 (not_93_out, OP5);
  not not_94 (not_94_out, OP6);
  not not_95 (not_95_out, F25);
  not not_96 (not_96_out, OP2);
  not not_97 (not_97_out, OP3);
  not not_98 (not_98_out, OP5);
  not not_99 (not_99_out, OP6);
  not not_100 (not_100_out, OP3);
  not not_101 (not_101_out, OP6);
  not not_102 (not_102_out, F25);
  not not_103 (not_103_out, F30);
  not not_104 (not_104_out, OP4);
  not not_105 (not_105_out, F12);
  not not_106 (not_106_out, F13);
  not not_107 (not_107_out, F14);
  not not_108 (not_108_out, OP3);
  not not_109 (not_109_out, OP6);
  not not_110 (not_110_out, OP4);
  not not_111 (not_111_out, OP2);
  not not_112 (not_112_out, OP3);
  not not_113 (not_113_out, F12);
  not not_114 (not_114_out, F13);
  not not_115 (not_115_out, F14);
  not not_116 (not_116_out, F25);
  not not_117 (not_117_out, F30);
  not not_118 (not_118_out, OP2);
  not not_119 (not_119_out, OP3);
  not not_120 (not_120_out, OP4);
  not not_121 (not_121_out, OP6);
  not not_122 (not_122_out, F12);
  not not_123 (not_123_out, F14);
  not not_124 (not_124_out, OP2);
  not not_125 (not_125_out, OP3);
  not not_126 (not_126_out, OP4);
  not not_127 (not_127_out, F12);
  not not_128 (not_128_out, F13);
  not not_129 (not_129_out, F14);
  not not_130 (not_130_out, OP2);
  not not_131 (not_131_out, OP3);
  not not_132 (not_132_out, OP4);
  not not_133 (not_133_out, F13);
  not not_134 (not_134_out, F14);
  not not_135 (not_135_out, OP3);
  not not_136 (not_136_out, OP4);
  not not_137 (not_137_out, F12);
  not not_138 (not_138_out, F13);
  not not_139 (not_139_out, F14);
  not not_140 (not_140_out, OP4);
  not not_141 (not_141_out, OP3);
  not not_142 (not_142_out, OP6);
  not not_143 (not_143_out, OP2);
  not not_144 (not_144_out, OP3);
  not not_145 (not_145_out, OP4);
  not not_146 (not_146_out, OP5);
  not not_147 (not_147_out, OP6);
  not not_148 (not_148_out, F12);
  not not_149 (not_149_out, F13);
  not not_150 (not_150_out, OP2);
  not not_151 (not_151_out, OP3);
  not not_152 (not_152_out, OP4);
  not not_153 (not_153_out, F13);
  and and_1 (and_1_out, not_1_out, not_2_out, not_3_out, not_4_out, not_5_out, not_6_out, not_7_out, F14);
  and and_2 (and_2_out, not_8_out, not_9_out, not_10_out, not_11_out, not_12_out, not_13_out, F13, not_14_out);
  and and_3 (MemWrite, not_15_out, not_16_out, not_17_out, OP5, not_18_out, not_19_out, F13, not_20_out);
  and and_4 (and_4_out, not_21_out, not_22_out, not_23_out, not_24_out, not_25_out, not_26_out, F14);
  and and_5 (and_5_out, not_27_out, not_28_out, not_29_out, not_30_out, not_31_out, F13, not_32_out);
  and and_6 (and_6_out, not_33_out, not_34_out, OP4, not_35_out, not_36_out, not_37_out);
  and and_7 (and_7_out, not_38_out, not_39_out, OP4, not_40_out, not_41_out, not_42_out, not_43_out, not_44_out);
  and and_8 (and_8_out, not_45_out, not_46_out, OP4, not_47_out, not_48_out, F14, not_49_out);
  and and_9 (and_9_out, not_50_out, not_51_out, OP4, not_52_out, not_53_out, F13, F14);
  and and_10 (and_10_out, not_54_out, not_55_out, not_56_out, not_57_out, not_58_out, not_59_out, F14);
  and and_11 (and_11_out, not_60_out, not_61_out, not_62_out, not_63_out, not_64_out, F13, not_65_out);
  and and_12 (and_12_out, not_66_out, not_67_out, OP4, not_68_out, not_69_out, not_70_out);
  and and_13 (and_13_out, not_71_out, not_72_out, OP4, not_73_out, not_74_out, not_75_out, not_76_out, not_77_out);
  and and_14 (and_14_out, not_78_out, not_79_out, OP4, not_80_out, not_81_out, not_82_out, not_83_out, not_84_out);
  and and_15 (and_15_out, not_85_out, not_86_out, OP4, not_87_out, not_88_out, not_89_out, not_90_out);
  and and_16 (and_16_out, not_91_out, not_92_out, OP4, not_93_out, not_94_out, F14, not_95_out);
  and and_17 (and_17_out, not_96_out, not_97_out, OP4, not_98_out, not_99_out, F13, F14);
  and and_18 (and_18_out, not_100_out, OP4, OP5, not_101_out, F13, not_102_out, not_103_out);
  and and_19 (and_19_out, OP2, not_104_out, OP5, OP6, not_105_out, not_106_out, not_107_out);
  and and_20 (and_20_out, OP2, not_108_out, OP4, OP5, not_109_out);
  and and_21 (and_21_out, OP2, OP3, not_110_out, OP5, OP6);
  and and_22 (ecall, not_111_out, not_112_out, OP4, OP5, OP6, not_113_out, not_114_out, not_115_out, not_116_out, not_117_out);
  and and_23 (S_Type, not_118_out, not_119_out, not_120_out, OP5, not_121_out, not_122_out, F13, not_123_out);
  and and_24 (BEQ, not_124_out, not_125_out, not_126_out, OP5, OP6, not_127_out, not_128_out, not_129_out);
  and and_25 (BNE, not_130_out, not_131_out, not_132_out, OP5, OP6, F12, not_133_out, not_134_out);
  and and_26 (JALR, OP2, not_135_out, not_136_out, OP5, OP6, not_137_out, not_138_out, not_139_out);
  and and_27 (JAL, OP2, OP3, not_140_out, OP5, OP6);
  and and_28 (LUI, OP2, not_141_out, OP4, OP5, not_142_out);
  and and_29 (LBU, not_143_out, not_144_out, not_145_out, not_146_out, not_147_out, not_148_out, not_149_out, F14);
  and and_30 (BGE, not_150_out, not_151_out, not_152_out, OP5, OP6, F12, not_153_out, F14);
  or or_1 (MemToReg, and_1_out, and_2_out);
  or or_2 (ALU_SRC, and_4_out, and_5_out, and_6_out, and_7_out, and_8_out, and_9_out);
  or or_3 (RegWrite, and_10_out, and_11_out, and_12_out, and_13_out, and_14_out, and_15_out, and_16_out, and_17_out, and_18_out, and_19_out, and_20_out, and_21_out);
endmodule

// ALU
module ALU (
  input  [31:0] X,
  input  [31:0] Y,
  input  [3:0] AluOP,
  output out_4,
  output Equal,
  output out_6,
  output [31:0] Result,
  output [31:0] Result_2
);

  wire [0:0] comparator_1_lt, comparator_2_lt;
  wire [31:0] adder_1_out, AND_out, divider_1_out, divider_1_rem, multiplier_1_cout, multiplier_1_out,
       NOR_out, OR_out, shifter_1_out, shifter_2_out, shifter_3_out, subtractor_1_out, XOR_out;

  assign AND_out = X & Y;  // AND_Gate AND, 32 bits wide
  assign OR_out = X | Y;  // OR_Gate OR, 32 bits wide
  Shifter #(.width(32), .shift("ll")) shifter_1 (.in(X), .\dist (Y[4:0]), .out(shifter_1_out));
  Shifter #(.width(32), .shift("ar")) shifter_2 (.in(X), .\dist (Y[4:0]), .out(shifter_2_out));
  Shifter #(.width(32), .shift("lr")) shifter_3 (.in(X), .\dist (Y[4:0]), .out(shifter_3_out));
  Multiplier #(.width(32)) multiplier_1 (.a(X), .b(Y), .out(multiplier_1_out), .cout(multiplier_1_cout));  // open: cin
  Divider #(.width(32)) divider_1 (.a(X), .b(Y), .out(divider_1_out), .rem(divider_1_rem));  // open: upper
  Adder #(.width(32)) adder_1 (.a(X), .b(Y), .out(adder_1_out));  // open: cin, cout
  Subtractor #(.width(32)) subtractor_1 (.a(X), .b(Y), .out(subtractor_1_out));  // open: bin, bout
  assign XOR_out = X ^ Y;  // XOR_Gate XOR, 32 bits wide
  assign NOR_out = ~(X | Y);  // NOR_Gate NOR, 32 bits wide
  Comparator #(.width(32), .mode("twosComplement")) comparator_1 (
    .a(X), .b(Y), .eq(Equal), .lt(comparator_1_lt[0]));  // open: gt
  Comparator #(.width(32), .mode("unsigned")) comparator_2 (.a(X), .b(Y), .lt(comparator_2_lt[0]));  // open: gt, eq
  Multiplexer #(.select(4), .width(32), .disabled("Z"), .enable("false")) multiplexer_1 (
    .in0(shifter_1_out), .in1(shifter_2_out), .in2(shifter_3_out), .in3(multiplier_1_out),
    .in4(divider_1_out), .in5(adder_1_out), .in6(subtractor_1_out), .in7(AND_out), .in8(OR_out),
    .in9(XOR_out), .in10(NOR_out), .in11({{31{1'b0}}, comparator_1_lt[0]}),
    .in12({{31{1'b0}}, comparator_2_lt[0]}), .in13({32{1'b0}}), .in14({32{1'b0}}), .in15({32{1'b0}}),
    .out(Result), .sel(AluOP));
  Multiplexer #(.select(4), .width(32), .disabled("Z"), .enable("false")) multiplexer_2 (
    .in0({32{1'b0}}), .in1({32{1'b0}}), .in2({32{1'b0}}), .in3(multiplier_1_cout), .in4(divider_1_rem),
    .in5({32{1'b0}}), .in6({32{1'b0}}), .in7({32{1'b0}}), .in8({32{1'b0}}), .in9({32{1'b0}}),
    .in10({32{1'b0}}), .in11({32{1'b0}}), .in12({32{1'b0}}), .in13({32{1'b0}}), .in14({32{1'b0}}),
    .in15({32{1'b0}}), .out(Result_2), .sel(AluOP));
  Multiplexer #(.select(4), .width(1), .disabled("Z"), .enable("false")) multiplexer_3 (
    .in0(1'b0), .in1(1'b0), .in2(1'b0), .in3(1'b0), .in4(1'b0), .in5(1'b0), .in6(1'b0), .in7(1'b0),
    .in8(1'b0), .in9(1'b0), .in10(1'b0), .in11(comparator_1_lt[0]), .in12(comparator_2_lt[0]), .in13(1'b0),
    .in14(1'b0), .in15(1'b0), .out(out_6), .sel(AluOP));
  not not_1 (out_4, out_6);

  // Other names for the same wires on the sheet: Result2[31:0] = Result_2; S[3:0] = AluOP; tunnel = out_6;
  //   tunnel_t = out_4

  // Notes on the sheet:
  //   不要改变此引脚区域内容，也不要改变ALU封装形式
  //   输入引脚
  //   输出引脚
endmodule

module Regifile (
  input  [31:0] Din,
  input  Clk,
  input  WE,
  input  [4:0] R1_num,
  input  [4:0] W_num,
  input  [4:0] R2_num,
  output [31:0] R1,
  output [31:0] R2
);

  // RegisterFile registerfile_1: pin names not known; wires that end beside it: Din, Clk, WE, W_num, R1_num, R2_num, R1, R2
endmodule

module \理想流水线  (
  output RegWrite,
  output MemWrite,
  output [31:0] IF_PC,
  output [31:0] ID_PC,
  output [31:0] EX_PC,
  output [31:0] M_PC,
  output [31:0] WB_PC,
  output [31:0] RDin,
  output [31:0] MDin,
  output [31:0] LedData
);

  wire alu_1_equal, alu_1_out_4, and_1_out, and_2_out, and_3_out, and_4_out, Bge, bjump, CLK, clock_1_out,
       clock_2_out, comparator_1_eq, comparator_1_lt, d_ff_1_q, Ecall, Equal, Go, halt, IR1, IR2, IR3, J,
       Jal, Jalr, Lbu, Lui, nand_1_out, not_1_out, not_2_out, not_3_out, RST, S, W1, W2, W3,
       \单周期硬布线控制器_1_alu_src , \单周期硬布线控制器_1_beq , \单周期硬布线控制器_1_bne , \单周期硬布线控制器_1_ecall ,
       \单周期硬布线控制器_1_memtoreg , \单周期硬布线控制器_1_memwrite , \单周期硬布线控制器_1_regwrite , \理想流水线ex_mem_1_ex_lbu ,
       \理想流水线ex_mem_1_ex_lui , \理想流水线ex_mem_1_mem_ecall , \理想流水线ex_mem_1_mem_equal , \理想流水线ex_mem_1_mem_jal ,
       \理想流水线ex_mem_1_mem_jalr , \理想流水线ex_mem_1_mem_memtoreg , \理想流水线ex_mem_1_mem_regwrite ,
       \理想流水线id_ex_1_ex_alusrcb , \理想流水线id_ex_1_ex_beq , \理想流水线id_ex_1_ex_bge , \理想流水线id_ex_1_ex_bne ,
       \理想流水线id_ex_1_ex_ecall , \理想流水线id_ex_1_ex_jal , \理想流水线id_ex_1_ex_jalr , \理想流水线id_ex_1_ex_lbu ,
       \理想流水线id_ex_1_ex_lui , \理想流水线id_ex_1_ex_memtoreg , \理想流水线id_ex_1_ex_memwrite ,
       \理想流水线id_ex_1_ex_regwrite , \理想流水线mem_wb_1_wb_jal , \理想流水线mem_wb_1_wb_jalr , \理想流水线mem_wb_1_wb_lui ,
       \理想流水线pc计算_1_bjrst , \理想流水线pc计算_1_jrst ;
  wire [3:0] \单周期硬布线控制器_1_alu_op , \理想流水线id_ex_1_ex_aluop ;
  wire [4:0] multiplexer_1_out, multiplexer_2_out, WB_rd, \理想流水线ex_mem_1_mem_rd , \理想流水线id_ex_1_ex_rd ;
  wire [11:0] multiplexer_3_out;
  wire [12:0] CNT_num;
  wire [15:0] \LoadUse次数 , \总周期数 , \插入气泡数 , \无条件分支数 , \条件分支成功数 ;
  wire [31:0] adder_1_out, adder_2_out, alu_1_result, bAddr, bit_extender_1_out, bit_extender_2_out,
       bit_extender_3_out, bit_extender_4_out, EX_IR, ID_IR, IF_IR, jAddr, LedShow, MEM_IR,
       multiplexer_4_out, multiplexer_5_out, multiplexer_6_out, multiplexer_7_out, multiplexer_8_out,
       ram_1_data, regifile_1_r1, regifile_1_r2, shifter_1_out, shifter_2_out, shifter_3_out, shifter_4_out,
       shifter_5_out, WB_IR, \理想流水线ex_mem_1_ex_imm_jal , \理想流水线ex_mem_1_ex_imm_lui ,
       \理想流水线ex_mem_1_mem_calc , \理想流水线id_ex_1_ex_a , \理想流水线id_ex_1_ex_imm , \理想流水线id_ex_1_ex_imm_jal ,
       \理想流水线id_ex_1_ex_imm_lui , \理想流水线mem_wb_1_wb_calc_mdout , \理想流水线mem_wb_1_wb_imm_jal ,
       \理想流水线mem_wb_1_wb_imm_lui , \理想流水线pc计算_1_npc ;

  Button \u_总复位  (.out(RST));
  Button _1 (.out(IR1));
  Button _2 (.out(IR2));
  Button _3 (.out(IR3));
  // Probe on \总周期数 
  // Probe on \总周期数 
  Button \u_继续运行  (.out(Go));
  LED #(.active("true")) led_1 (.in(W1));
  LED #(.active("true")) led_2 (.in(W2));
  LED #(.active("true")) led_3 (.in(W3));
  Hex_Digit_Display hex_digit_display_1 (.value(LedData[31:28]));  // open: dp
  // Probe on IF_PC[19:0]
  // RiscV_Probe riscv_probe_1: pin names not known; wires that end beside it: IF_IR
  Register #(.width(32), .trigger("rising"), .Select("low")) PC (
    .D(\理想流水线pc计算_1_npc ), .en(halt), .Q(IF_PC), .clk(CLK));  // open: clr
  Hex_Digit_Display hex_digit_display_2 (.value(LedData[23:20]));  // open: dp
  Hex_Digit_Display hex_digit_display_3 (.value(LedData[27:24]));  // open: dp
  // Probe on ID_PC[19:0]
  // RiscV_Probe riscv_probe_2: pin names not known; wires that end beside it: ID_IR
  Adder #(.width(32)) adder_1 (.a(IF_PC), .b(32'h4), .out(adder_1_out));  // open: cin, cout
  \理想流水线PC计算  \u_理想流水线pc计算_1  (
    .bJump(bjump), .J(J), .PC_4(adder_1_out), .bAddr(jAddr), .jAddr(bAddr), .Jrst(\理想流水线pc计算_1_jrst ),
    .NPC(\理想流水线pc计算_1_npc ), .BJRst(\理想流水线pc计算_1_bjrst ));
  Hex_Digit_Display hex_digit_display_4 (.value(LedData[15:12]));  // open: dp
  Hex_Digit_Display hex_digit_display_5 (.value(LedData[19:16]));  // open: dp
  Hex_Digit_Display hex_digit_display_6 (.value(LedData[11:8]));  // open: dp
  Hex_Digit_Display hex_digit_display_7 (.value(LedData[7:4]));  // open: dp
  Clock #(.highDuration(1), .lowDuration(1)) clock_1 (.out(clock_1_out));
  // Probe on EX_PC[19:0]
  // RiscV_Probe riscv_probe_3: pin names not known; wires that end beside it: clock_1_out, EX_IR, CLK
  ROM #(.addrWidth(10), .dataWidth(32), .Select("high")) rom_1 (.addr(IF_PC[11:2]), .data(IF_IR));
  Counter #(.width(16), .max('hffff), .ongoal("wrap"), .trigger("rising"), .behavior("old")) counter_1 (
    .count(halt), .Q(\总周期数 ), .clk(CLK));  // open: load, D, carry, clr, preset
  Hex_Digit_Display hex_digit_display_8 (.value(LedData[3:0]));  // open: dp
  \理想流水线IF_ID  \u_理想流水线if_id_1  (
    .IF_PC(IF_PC), .IF_IR(IF_IR), .clk(CLK), .halt(halt), .ID_PC(ID_PC), .ID_IR(ID_IR),
    .rst(\理想流水线pc计算_1_bjrst ));
  // Probe on \总周期数 
  // Probe on M_PC[19:0]
  // RiscV_Probe riscv_probe_4: pin names not known; wires that end beside it: MEM_IR
  Counter #(.width(16), .max('hffff), .ongoal("wrap"), .trigger("rising"), .behavior("old")) counter_2 (
    .count(and_1_out), .Q(\无条件分支数 ), .clk(CLK));  // open: load, D, carry, clr, preset
  and and_1 (and_1_out, halt, J);
  // Probe on \总周期数 
  // Probe on \无条件分支数 
  // Probe on \条件分支成功数 
  // Probe on \插入气泡数 
  // Probe on \LoadUse次数 
  \单周期硬布线控制器  \u_单周期硬布线控制器_1  (
    .Funct({ID_IR[30], ID_IR[25], ID_IR[14:12]}), .OP(ID_IR[6:2]), .ALU_OP(\单周期硬布线控制器_1_alu_op ),
    .MemToReg(\单周期硬布线控制器_1_memtoreg ), .MemWrite(\单周期硬布线控制器_1_memwrite ), .ALU_SRC(\单周期硬布线控制器_1_alu_src ),
    .RegWrite(\单周期硬布线控制器_1_regwrite ), .ecall(\单周期硬布线控制器_1_ecall ), .S_type(S), .Jalr(Jalr),
    .Beq(\单周期硬布线控制器_1_beq ), .JAL(Jal), .Bne(\单周期硬布线控制器_1_bne ), .Lui(Lui), .Lbu(Lbu), .Bge(Bge));
  assign bit_extender_1_out = {{12{ID_IR[31]}}, ID_IR[31:12]};  // Bit_Extender bit_extender_1
  // Probe on IF_PC[11:0]
  // Probe on WB_PC[19:0]
  // RiscV_Probe riscv_probe_5: pin names not known; wires that end beside it: WB_IR
  Multiplexer #(.select(1), .width(5), .disabled("Z"), .enable("false")) multiplexer_1 (
    .in0(ID_IR[19:15]), .in1(5'b10001), .out(multiplexer_1_out), .sel(\单周期硬布线控制器_1_ecall ));
  Multiplexer #(.select(1), .width(5), .disabled("Z"), .enable("false")) multiplexer_2 (
    .in0(ID_IR[24:20]), .in1(5'b01010), .out(multiplexer_2_out), .sel(\单周期硬布线控制器_1_ecall ));
  Shifter #(.width(32), .shift("ll")) shifter_1 (.in(bit_extender_1_out), .\dist (5'b01100), .out(shifter_1_out));
  assign bit_extender_2_out = {{12{ID_IR[31]}}, {ID_IR[31], ID_IR[19:12], ID_IR[20], ID_IR[30:21]}};  // Bit_Extender bit_extender_2
  and and_2 (and_2_out, halt, bjump);
  // Probe on EX_PC[11:0]
  // Probe on ID_PC[11:0]
  Regifile regifile_1 (
    .Din(RDin), .Clk(CLK), .R1(regifile_1_r1), .R2(regifile_1_r2), .WE(RegWrite), .W_num(WB_rd),
    .R1_num(multiplexer_1_out), .R2_num(multiplexer_2_out));
  assign bit_extender_3_out = {{20{multiplexer_3_out[11]}}, multiplexer_3_out};  // Bit_Extender bit_extender_3
  Multiplexer #(.select(1), .width(12), .disabled("Z"), .enable("false")) multiplexer_3 (
    .in0(ID_IR[31:20]), .in1({ID_IR[31:25], ID_IR[11:7]}), .out(multiplexer_3_out), .sel(S));
  assign bit_extender_4_out = {{20{ID_IR[31]}}, {ID_IR[31], ID_IR[7], ID_IR[30:25], ID_IR[11:8]}};  // Bit_Extender bit_extender_4
  Shifter #(.width(32), .shift("ll")) shifter_2 (.in(bit_extender_2_out), .\dist (5'b00001), .out(shifter_2_out));
  Counter #(.width(16), .max('hffff), .ongoal("wrap"), .trigger("rising"), .behavior("old")) counter_3 (
    .count(and_2_out), .Q(\条件分支成功数 ), .clk(CLK));  // open: load, D, carry, clr, preset
  // Probe on M_PC[11:0]
  D_Flip_Flop #(.trigger("high"), .Pre_Clr_Positions("LEGACY"), .NegatePresetClear("false"), .enable("true"), .NewFFLayout("false")) d_ff_1 (.Q(d_ff_1_q));  // open: clk, D, Qn, preset, en, reset
  // Probe on 13'hc
  Shifter #(.width(32), .shift("ll")) shifter_3 (.in(bit_extender_4_out), .\dist (5'b00001), .out(shifter_3_out));
  // Probe on WB_PC[11:0]
  Comparator #(.width(13), .mode("twosComplement")) comparator_1 (
    .a(CNT_num), .b(13'hc), .eq(comparator_1_eq), .lt(comparator_1_lt));  // open: gt
  Clock #(.highDuration(1), .lowDuration(1)) clock_2 (.out(clock_2_out));
  nand nand_1 (nand_1_out, d_ff_1_q, comparator_1_eq);
  Counter #(.width(13), .max('h1fff), .ongoal("stay"), .trigger("rising"), .behavior("old")) counter_4 (
    .count(comparator_1_lt), .Q(CNT_num), .clk(clock_2_out));  // open: load, D, carry, clr, preset
  \理想流水线ID_EX  \u_理想流水线id_ex_1  (
    .ID_PC(ID_PC), .ID_MemToReg(\单周期硬布线控制器_1_memtoreg ), .ID_MemWrite(\单周期硬布线控制器_1_memwrite ),
    .ID_AluOP(\单周期硬布线控制器_1_alu_op ), .ID_AluSrcB(\单周期硬布线控制器_1_alu_src ), .ID_Ecall(\单周期硬布线控制器_1_ecall ),
    .ID_R1(regifile_1_r1), .ID_R2(regifile_1_r2), .ID_imm(bit_extender_3_out), .clk(CLK), .halt(halt),
    .EX_PC(EX_PC), .EX_MemToReg(\理想流水线id_ex_1_ex_memtoreg ), .EX_MemWrite(\理想流水线id_ex_1_ex_memwrite ),
    .EX_AluOP(\理想流水线id_ex_1_ex_aluop ), .EX_AluSrcB(\理想流水线id_ex_1_ex_alusrcb ),
    .EX_Ecall(\理想流水线id_ex_1_ex_ecall ), .EX_A(\理想流水线id_ex_1_ex_a ), .EX_B(LedShow),
    .EX_imm(\理想流水线id_ex_1_ex_imm ), .rst(\理想流水线pc计算_1_bjrst ), .ID_IR(ID_IR), .EX_IR(EX_IR),
    .ID_Beq(\单周期硬布线控制器_1_beq ), .EX_Beq(\理想流水线id_ex_1_ex_beq ), .ID_Bne(\单周期硬布线控制器_1_bne ),
    .EX_Bne(\理想流水线id_ex_1_ex_bne ), .ID_RegWrite(\单周期硬布线控制器_1_regwrite ),
    .EX_RegWrite(\理想流水线id_ex_1_ex_regwrite ), .ID_rd(ID_IR[11:7]), .EX_rd(\理想流水线id_ex_1_ex_rd ),
    .ID_Jal(Jal), .ID_Jalr(Jalr), .EX_Jal(\理想流水线id_ex_1_ex_jal ), .EX_Jalr(\理想流水线id_ex_1_ex_jalr ),
    .ID_Bge(Bge), .EX_Bge(\理想流水线id_ex_1_ex_bge ), .ID_imm_Lui(shifter_1_out),
    .EX_imm_Lui(\理想流水线id_ex_1_ex_imm_lui ), .ID_Lui(Lui), .EX_Lui(\理想流水线id_ex_1_ex_lui ), .ID_Lbu(Lbu),
    .EX_Lbu(\理想流水线id_ex_1_ex_lbu ), .ID_imm_Jal(shifter_2_out), .EX_imm_Jal(\理想流水线id_ex_1_ex_imm_jal ),
    .ID_imm_B(shifter_3_out), .EX_imm_B(bAddr));
  assign CLK = nand_1_out ? clock_2_out : 1'bz;  // Controlled_Buffer controlled_buffer_1
  Multiplexer #(.select(1), .width(32), .disabled("Z"), .enable("false")) multiplexer_4 (
    .in0(LedShow), .in1(\理想流水线id_ex_1_ex_imm ), .out(multiplexer_4_out), .sel(\理想流水线id_ex_1_ex_alusrcb ));
  Pull_Resistor #(.pull(1)) pull_resistor_1 (.node(CLK));
  Multiplexer #(.select(1), .width(32), .disabled("Z"), .enable("false")) multiplexer_5 (
    .in0(multiplexer_4_out), .in1(32'ha), .out(multiplexer_5_out), .sel(\理想流水线id_ex_1_ex_ecall ));
  not not_1 (not_1_out, Equal);
  ALU alu_1 (
    .X(\理想流水线id_ex_1_ex_a ), .Y(multiplexer_5_out), .AluOP(\理想流水线id_ex_1_ex_aluop ), .Equal(alu_1_equal),
    .Result(alu_1_result), .out_4(alu_1_out_4));  // open: Result_2, out_6
  not not_2 (not_2_out, and_3_out);
  and and_3 (and_3_out, Ecall, Equal);
  and and_4 (and_4_out, Ecall, not_1_out);
  \理想流水线分支逻辑设计  \u_理想流水线分支逻辑设计_1  (
    .Bge(\理想流水线id_ex_1_ex_bge ), .in_2(alu_1_equal), .Beq(\理想流水线id_ex_1_ex_beq ), .in_4(alu_1_out_4),
    .Bne(\理想流水线id_ex_1_ex_bne ), .branch(bjump));
  or or_1 (halt, Go, not_2_out);
  Register #(.width(32), .trigger("rising"), .Select("low")) register_1 (
    .D(LedShow), .en(and_4_out), .Q(LedData), .clk(CLK));  // open: clr
  \理想流水线EX_MEM  \u_理想流水线ex_mem_1  (
    .EX_PC(EX_PC), .EX_MemToReg(\理想流水线id_ex_1_ex_memtoreg ), .EX_MemWrite(\理想流水线id_ex_1_ex_memwrite ),
    .EX_MDin(LedShow), .EX_Calc(alu_1_result), .clk(CLK), .halt(halt), .MEM_PC(M_PC),
    .MEM_MemToReg(\理想流水线ex_mem_1_mem_memtoreg ), .MEM_MemWrite(MemWrite), .MEM_MDin(MDin),
    .MEM_Calc(\理想流水线ex_mem_1_mem_calc ), .rst(\理想流水线pc计算_1_jrst ), .EX_IR(EX_IR), .MEM_IR(MEM_IR),
    .EX_RegWrite(\理想流水线id_ex_1_ex_regwrite ), .MEM_RegWrite(\理想流水线ex_mem_1_mem_regwrite ),
    .EX_rd(\理想流水线id_ex_1_ex_rd ), .Mem_Rd(\理想流水线ex_mem_1_mem_rd ), .EX_Ecall(\理想流水线id_ex_1_ex_ecall ),
    .MEM_Ecall(\理想流水线ex_mem_1_mem_ecall ), .EX_Equal(alu_1_equal), .MEM_Equal(\理想流水线ex_mem_1_mem_equal ),
    .EX_Jal(\理想流水线id_ex_1_ex_jal ), .MEM_Jal(\理想流水线ex_mem_1_mem_jal ), .EX_Jalr(\理想流水线id_ex_1_ex_jalr ),
    .MEM_Jalr(\理想流水线ex_mem_1_mem_jalr ), .ID_imm_Jal(\理想流水线id_ex_1_ex_imm_jal ),
    .EX_imm_Jal(\理想流水线ex_mem_1_ex_imm_jal ), .ID_Lui(\理想流水线id_ex_1_ex_lui ), .EX_Lui(\理想流水线ex_mem_1_ex_lui ),
    .ID_Lbu(\理想流水线id_ex_1_ex_lbu ), .EX_Lbu(\理想流水线ex_mem_1_ex_lbu ), .ID_imm_Lui(\理想流水线id_ex_1_ex_imm_lui ),
    .EX_imm_Lui(\理想流水线ex_mem_1_ex_imm_lui ));
  not not_3 (not_3_out, MemWrite);
  RAM #(.addrWidth(10), .dataWidth(32), .bus("separate"), .Select("high")) ram_1 (
    .addr(\理想流水线ex_mem_1_mem_calc [11:2]), .din(MDin), .data(ram_1_data), .str(MemWrite), .clk(CLK),
    .ld(not_3_out));  // open: sel, clr
  Multiplexer #(.select(1), .width(32), .disabled("Z"), .enable("false")) multiplexer_6 (
    .in0(\理想流水线ex_mem_1_mem_calc ), .in1(ram_1_data), .out(multiplexer_6_out),
    .sel(\理想流水线ex_mem_1_mem_memtoreg ));
  Shifter #(.width(32), .shift("ll")) shifter_4 (.in(multiplexer_6_out), .\dist (5'b11000), .out(shifter_4_out));
  Shifter #(.width(32), .shift("lr")) shifter_5 (.in(shifter_4_out), .\dist (5'b11000), .out(shifter_5_out));
  Multiplexer #(.select(1), .width(32), .disabled("Z"), .enable("false")) multiplexer_7 (
    .in0(multiplexer_6_out), .in1(shifter_5_out), .out(multiplexer_7_out), .sel(\理想流水线ex_mem_1_ex_lbu ));
  \理想流水线MEM_WB  \u_理想流水线mem_wb_1  (
    .MEM_PC(M_PC), .MEM_IR(MEM_IR), .MEM_Lui(\理想流水线ex_mem_1_ex_lui ),
    .MEM_RegWrite(\理想流水线ex_mem_1_mem_regwrite ), .MEM_Jal(\理想流水线ex_mem_1_mem_jal ),
    .MEM_Jalr(\理想流水线ex_mem_1_mem_jalr ), .Mem_Clac_MDout(multiplexer_7_out),
    .MEM_imm_Jal(\理想流水线ex_mem_1_ex_imm_jal ), .MEM_Rd(\理想流水线ex_mem_1_mem_rd ),
    .MEM_imm_Lui(\理想流水线ex_mem_1_ex_imm_lui ), .clk(CLK), .halt(halt), .WB_PC(WB_PC), .WB_IR(WB_IR),
    .WB_Lui(\理想流水线mem_wb_1_wb_lui ), .WB_RegWrite(RegWrite), .WB_Jal(\理想流水线mem_wb_1_wb_jal ),
    .WB_Jalr(\理想流水线mem_wb_1_wb_jalr ), .WB_Calc_MDout(\理想流水线mem_wb_1_wb_calc_mdout ),
    .WB_imm_Jal(\理想流水线mem_wb_1_wb_imm_jal ), .WB_Rd(WB_rd), .WB_imm_Lui(\理想流水线mem_wb_1_wb_imm_lui ),
    .rst(\理想流水线pc计算_1_jrst ), .MEM_Equal(\理想流水线ex_mem_1_mem_equal ), .WB_Equal(Equal),
    .MEM_Ecall(\理想流水线ex_mem_1_mem_ecall ), .WB_Ecall(Ecall));
  Adder #(.width(32)) adder_2 (.a(WB_PC), .b(32'h4), .out(adder_2_out));  // open: cin, cout
  Multiplexer #(.select(1), .width(32), .disabled("Z"), .enable("false")) multiplexer_8 (
    .in0(\理想流水线mem_wb_1_wb_calc_mdout ), .in1(\理想流水线mem_wb_1_wb_imm_lui ), .out(multiplexer_8_out),
    .sel(\理想流水线mem_wb_1_wb_lui ));
  and and_5 (J, \理想流水线mem_wb_1_wb_jal , \理想流水线mem_wb_1_wb_jalr );
  Multiplexer #(.select(1), .width(32), .disabled("Z"), .enable("false")) multiplexer_9 (
    .in0(multiplexer_8_out), .in1(adder_2_out), .out(RDin), .sel(J));
  \理想流水线跳转逻辑设计  \u_理想流水线跳转逻辑设计_1  (
    .JAL(\理想流水线mem_wb_1_wb_jal ), .JALR(\理想流水线mem_wb_1_wb_jalr ), .JALR_Addr(\理想流水线mem_wb_1_wb_calc_mdout ),
    .JAL_Addr(\理想流水线mem_wb_1_wb_imm_jal ), .J_Addr(jAddr));

  // Other names for the same wires on the sheet: rd[4:0] = ID_IR[11:7]; MEM_PC[31:0] = M_PC

  // Notes on the sheet:
  //   中断源
  //   时空图监测，可删除
  //   中断等待指示
  //   数码管输出
  //   指令存储器
  //   contents of rom_1 (hex, n*v repeats v):
  //   413 493 913 993 46413 14e493 296913 39e993 842023 942223 1242423 1342623 a00893 493 913 993 73
  //   rs1
  //   rs2
  //   rd
  //   imm20 LUI
  //   imm20 Jal
  //   imm12 I
  //   imm12 S
  //   周期数、分支数记录
  //   控制位
  //   流水调试日志用
  //   暂停节拍，不能为0
  //   戳工具置1进入计数暂停模式，ctrl+k时钟自动运行到对应节拍暂停
  //   ctrl+k关闭时钟连续运行，将控制位置零，进入单步调试模式调试
  //   用这个时钟源需要去掉电路中的其他时钟源
  //   可计数暂停的时钟源
  //   Ecall选项
  //   为方便自动评测，需要输出流水线各段保存的PC值，注意是PC不是PC+4，另外ID段寄存器写入信息，Mem段内存写入信息也要输出
  //   数据存储器
endmodule

// IF/ID
module \理想流水线IF_ID  (
  input  [31:0] IF_PC,
  input  [31:0] IF_IR,
  input  clk,
  input  rst,
  input  halt,
  output [31:0] ID_PC,
  output [31:0] ID_IR
);

  Register #(.width(32), .trigger("rising"), .Select("low")) PC (.D(IF_PC), .en(halt), .Q(ID_PC), .clk(clk), .clr(rst));
  Register #(.width(32), .trigger("rising"), .Select("low")) IR (.D(IF_IR), .en(halt), .Q(ID_IR), .clk(clk), .clr(rst));
endmodule

// ID/EX
module \理想流水线ID_EX  (
  input  [31:0] ID_PC,
  input  [31:0] ID_IR,
  input  ID_Bge,
  input  ID_Beq,
  input  ID_Bne,
  input  ID_MemToReg,
  input  ID_MemWrite,
  input  [3:0] ID_AluOP,
  input  ID_AluSrcB,
  input  ID_RegWrite,
  input  ID_Jal,
  input  ID_Jalr,
  input  [4:0] ID_rd,
  input  ID_Ecall,
  input  [31:0] ID_R1,
  input  [31:0] ID_R2,
  input  [31:0] ID_imm,
  input  [31:0] ID_imm_B,
  input  [31:0] ID_imm_Jal,
  input  ID_Lui,
  input  ID_Lbu,
  input  [31:0] ID_imm_Lui,
  input  clk,
  input  rst,
  input  halt,
  output [31:0] EX_PC,
  output [31:0] EX_IR,
  output EX_Bge,
  output EX_Beq,
  output EX_Bne,
  output EX_MemToReg,
  output EX_MemWrite,
  output [3:0] EX_AluOP,
  output EX_AluSrcB,
  output EX_RegWrite,
  output EX_Jal,
  output EX_Jalr,
  output [4:0] EX_rd,
  output EX_Ecall,
  output [31:0] EX_A,
  output [31:0] EX_B,
  output [31:0] EX_imm,
  output [31:0] EX_imm_B,
  output [31:0] EX_imm_Jal,
  output EX_Lui,
  output EX_Lbu,
  output [31:0] EX_imm_Lui
);

  Register #(.width(32), .trigger("rising"), .Select("low")) register_1 (
    .D(ID_PC), .en(halt), .Q(EX_PC), .clk(clk), .clr(rst));
  Register #(.width(32), .trigger("rising"), .Select("low")) register_2 (
    .D(ID_IR), .en(halt), .Q(EX_IR), .clk(clk), .clr(rst));
  Register #(.width(1), .trigger("rising"), .Select("low")) register_3 (
    .D(ID_Bge), .en(halt), .Q(EX_Bge), .clk(clk), .clr(rst));
  Register #(.width(1), .trigger("rising"), .Select("low")) register_4 (
    .D(ID_Beq), .en(halt), .Q(EX_Beq), .clk(clk), .clr(rst));
  Register #(.width(1), .trigger("rising"), .Select("low")) register_5 (
    .D(ID_Bne), .en(halt), .Q(EX_Bne), .clk(clk), .clr(rst));
  Register #(.width(1), .trigger("rising"), .Select("low")) register_6 (
    .D(ID_MemToReg), .en(halt), .Q(EX_MemToReg), .clk(clk), .clr(rst));
  Register #(.width(1), .trigger("rising"), .Select("low")) register_7 (
    .D(ID_MemWrite), .en(halt), .Q(EX_MemWrite), .clk(clk), .clr(rst));
  Register #(.width(4), .trigger("rising"), .Select("low")) register_8 (
    .D(ID_AluOP), .en(halt), .Q(EX_AluOP), .clk(clk), .clr(rst));
  Register #(.width(1), .trigger("rising"), .Select("low")) register_9 (
    .D(ID_AluSrcB), .en(halt), .Q(EX_AluSrcB), .clk(clk), .clr(rst));
  Register #(.width(1), .trigger("rising"), .Select("low")) register_10 (
    .D(ID_RegWrite), .en(halt), .Q(EX_RegWrite), .clk(clk), .clr(rst));
  Register #(.width(1), .trigger("rising"), .Select("low")) register_11 (
    .D(ID_Jal), .en(halt), .Q(EX_Jal), .clk(clk), .clr(rst));
  Register #(.width(1), .trigger("rising"), .Select("low")) register_12 (
    .D(ID_Jalr), .en(halt), .Q(EX_Jalr), .clk(clk), .clr(rst));
  Register #(.width(5), .trigger("rising"), .Select("low")) register_13 (
    .D(ID_rd), .en(halt), .Q(EX_rd), .clk(clk), .clr(rst));
  Register #(.width(1), .trigger("rising"), .Select("low")) register_14 (
    .D(ID_Ecall), .en(halt), .Q(EX_Ecall), .clk(clk), .clr(rst));
  Register #(.width(32), .trigger("rising"), .Select("low")) register_15 (
    .D(ID_R1), .en(halt), .Q(EX_A), .clk(clk), .clr(rst));
  Register #(.width(32), .trigger("rising"), .Select("low")) register_16 (
    .D(ID_R2), .en(halt), .Q(EX_B), .clk(clk), .clr(rst));
  Register #(.width(32), .trigger("rising"), .Select("low")) register_17 (
    .D(ID_imm), .en(halt), .Q(EX_imm), .clk(clk), .clr(rst));
  Register #(.width(32), .trigger("rising"), .Select("low")) register_18 (
    .D(ID_imm_B), .en(halt), .Q(EX_imm_B), .clk(clk), .clr(rst));
  Register #(.width(32), .trigger("rising"), .Select("low")) register_19 (
    .D(ID_imm_Jal), .en(halt), .Q(EX_imm_Jal), .clk(clk), .clr(rst));
  Register #(.width(1), .trigger("rising"), .Select("low")) register_20 (
    .D(ID_Lui), .en(halt), .Q(EX_Lui), .clk(clk), .clr(rst));
  Register #(.width(1), .trigger("rising"), .Select("low")) register_21 (
    .D(ID_Lbu), .en(halt), .Q(EX_Lbu), .clk(clk), .clr(rst));
  Register #(.width(32), .trigger("rising"), .Select("low")) register_22 (
    .D(ID_imm_Lui), .en(halt), .Q(EX_imm_Lui), .clk(clk), .clr(rst));
endmodule

// EX/MEM
module \理想流水线EX_MEM  (
  input  [31:0] EX_PC,
  input  [31:0] EX_IR,
  input  EX_MemToReg,
  input  EX_MemWrite,
  input  EX_RegWrite,
  input  EX_Jal,
  input  EX_Jalr,
  input  [31:0] EX_MDin,
  input  [31:0] EX_Calc,
  input  [4:0] EX_rd,
  input  EX_Ecall,
  input  EX_Equal,
  input  [31:0] ID_imm_Jal,
  input  ID_Lui,
  input  ID_Lbu,
  input  [31:0] ID_imm_Lui,
  input  clk,
  input  rst,
  input  halt,
  output [31:0] MEM_PC,
  output [31:0] MEM_IR,
  output MEM_MemToReg,
  output MEM_MemWrite,
  output MEM_RegWrite,
  output MEM_Jal,
  output MEM_Jalr,
  output [31:0] MEM_MDin,
  output [31:0] MEM_Calc,
  output [4:0] Mem_Rd,
  output MEM_Ecall,
  output MEM_Equal,
  output [31:0] EX_imm_Jal,
  output EX_Lui,
  output EX_Lbu,
  output [31:0] EX_imm_Lui
);

  Register #(.width(32), .trigger("rising"), .Select("low")) register_1 (
    .D(EX_PC), .en(halt), .Q(MEM_PC), .clk(clk), .clr(rst));
  Register #(.width(32), .trigger("rising"), .Select("low")) register_2 (
    .D(EX_IR), .en(halt), .Q(MEM_IR), .clk(clk), .clr(rst));
  Register #(.width(1), .trigger("rising"), .Select("low")) register_3 (
    .D(EX_MemToReg), .en(halt), .Q(MEM_MemToReg), .clk(clk), .clr(rst));
  Register #(.width(1), .trigger("rising"), .Select("low")) register_4 (
    .D(EX_MemWrite), .en(halt), .Q(MEM_MemWrite), .clk(clk), .clr(rst));
  Register #(.width(1), .trigger("rising"), .Select("low")) register_5 (
    .D(EX_RegWrite), .en(halt), .Q(MEM_RegWrite), .clk(clk), .clr(rst));
  Register #(.width(1), .trigger("rising"), .Select("low")) register_6 (
    .D(EX_Jal), .en(halt), .Q(MEM_Jal), .clk(clk), .clr(rst));
  Register #(.width(1), .trigger("rising"), .Select("low")) register_7 (
    .D(EX_Jalr), .en(halt), .Q(MEM_Jalr), .clk(clk), .clr(rst));
  Register #(.width(32), .trigger("rising"), .Select("low")) register_8 (
    .D(EX_MDin), .en(halt), .Q(MEM_MDin), .clk(clk), .clr(rst));
  Register #(.width(32), .trigger("rising"), .Select("low")) register_9 (
    .D(EX_Calc), .en(halt), .Q(MEM_Calc), .clk(clk), .clr(rst));
  Register #(.width(5), .trigger("rising"), .Select("low")) register_10 (
    .D(EX_rd), .en(halt), .Q(Mem_Rd), .clk(clk), .clr(rst));
  Register #(.width(1), .trigger("rising"), .Select("low")) register_11 (
    .D(EX_Ecall), .en(halt), .Q(MEM_Ecall), .clk(clk), .clr(rst));
  Register #(.width(1), .trigger("rising"), .Select("low")) register_12 (
    .D(EX_Equal), .en(halt), .Q(MEM_Equal), .clk(clk), .clr(rst));
  Register #(.width(32), .trigger("rising"), .Select("low")) register_13 (
    .D(ID_imm_Jal), .en(halt), .Q(EX_imm_Jal), .clk(clk), .clr(rst));
  Register #(.width(1), .trigger("rising"), .Select("low")) register_14 (
    .D(ID_Lui), .en(halt), .Q(EX_Lui), .clk(clk), .clr(rst));
  Register #(.width(1), .trigger("rising"), .Select("low")) register_15 (
    .D(ID_Lbu), .en(halt), .Q(EX_Lbu), .clk(clk), .clr(rst));
  Register #(.width(32), .trigger("rising"), .Select("low")) register_16 (
    .D(ID_imm_Lui), .en(halt), .Q(EX_imm_Lui), .clk(clk), .clr(rst));
endmodule

// MEM/WB
module \理想流水线MEM_WB  (
  input  [31:0] MEM_PC,
  input  [31:0] MEM_IR,
  input  MEM_Lui,
  input  MEM_RegWrite,
  input  MEM_Jal,
  input  MEM_Jalr,
  input  [31:0] Mem_Clac_MDout,
  input  [31:0] MEM_imm_Jal,
  input  [4:0] MEM_Rd,
  input  MEM_Equal,
  input  MEM_Ecall,
  input  [31:0] MEM_imm_Lui,
  input  clk,
  input  rst,
  input  halt,
  output [31:0] WB_PC,
  output [31:0] WB_IR,
  output WB_Lui,
  output WB_RegWrite,
  output WB_Jal,
  output WB_Jalr,
  output [31:0] WB_Calc_MDout,
  output [31:0] WB_imm_Jal,
  output [4:0] WB_Rd,
  output WB_Equal,
  output WB_Ecall,
  output [31:0] WB_imm_Lui
);

  Register #(.width(32), .trigger("rising"), .Select("low")) register_1 (
    .D(MEM_PC), .en(halt), .Q(WB_PC), .clk(clk), .clr(rst));
  Register #(.width(32), .trigger("rising"), .Select("low")) register_2 (
    .D(MEM_IR), .en(halt), .Q(WB_IR), .clk(clk), .clr(rst));
  Register #(.width(1), .trigger("rising"), .Select("low")) register_3 (
    .D(MEM_Lui), .en(halt), .Q(WB_Lui), .clk(clk), .clr(rst));
  Register #(.width(1), .trigger("rising"), .Select("low")) register_4 (
    .D(MEM_RegWrite), .en(halt), .Q(WB_RegWrite), .clk(clk), .clr(rst));
  Register #(.width(1), .trigger("rising"), .Select("low")) register_5 (
    .D(MEM_Jal), .en(halt), .Q(WB_Jal), .clk(clk), .clr(rst));
  Register #(.width(1), .trigger("rising"), .Select("low")) register_6 (
    .D(MEM_Jalr), .en(halt), .Q(WB_Jalr), .clk(clk), .clr(rst));
  Register #(.width(32), .trigger("rising"), .Select("low")) register_7 (
    .D(Mem_Clac_MDout), .en(halt), .Q(WB_Calc_MDout), .clk(clk), .clr(rst));
  Register #(.width(32), .trigger("rising"), .Select("low")) register_8 (
    .D(MEM_imm_Jal), .en(halt), .Q(WB_imm_Jal), .clk(clk), .clr(rst));
  Register #(.width(5), .trigger("rising"), .Select("low")) register_9 (
    .D(MEM_Rd), .en(halt), .Q(WB_Rd), .clk(clk), .clr(rst));
  Register #(.width(1), .trigger("rising"), .Select("low")) register_10 (
    .D(MEM_Equal), .en(halt), .Q(WB_Equal), .clk(clk), .clr(rst));
  Register #(.width(1), .trigger("rising"), .Select("low")) register_11 (
    .D(MEM_Ecall), .en(halt), .Q(WB_Ecall), .clk(clk), .clr(rst));
  Register #(.width(32), .trigger("rising"), .Select("low")) register_12 (
    .D(MEM_imm_Lui), .en(halt), .Q(WB_imm_Lui), .clk(clk), .clr(rst));
endmodule

// branch\n test
module \理想流水线分支逻辑设计  (
  input  Bge,
  input  in_2,
  input  Beq,
  input  in_4,
  input  Bne,
  output branch
);

  wire and_1_out, and_2_out, and_3_out, not_1_out;

  not not_1 (not_1_out, in_2);
  and and_1 (and_1_out, Bge, in_2);
  and and_2 (and_2_out, not_1_out, Beq);
  and and_3 (and_3_out, in_4, Bne);
  or or_1 (branch, and_1_out, and_2_out, and_3_out);
endmodule

// Jump\n Addr
module \理想流水线跳转逻辑设计  (
  input  JAL,
  input  JALR,
  input  [31:0] JALR_Addr,
  input  [31:0] JAL_Addr,
  output [31:0] J_Addr
);

  Multiplexer #(.select(1), .width(32), .disabled("Z"), .enable("false")) multiplexer_1 (
    .in0(JALR_Addr), .in1(JAL_Addr), .out(J_Addr), .sel(JAL));
endmodule

// New PC
module \理想流水线PC计算  (
  input  bJump,
  input  J,
  input  [31:0] PC_4,
  input  [31:0] bAddr,
  input  [31:0] jAddr,
  output Jrst,
  output BJRst,
  output [31:0] NPC
);

  wire and_1_out;
  wire [31:0] multiplexer_1_out;

  Multiplexer #(.select(1), .width(32), .disabled("Z"), .enable("false")) multiplexer_1 (
    .in0(bAddr), .in1(jAddr), .out(multiplexer_1_out), .sel(J));
  and and_1 (and_1_out, J, bJump);
  Multiplexer #(.select(1), .width(32), .disabled("Z"), .enable("false")) multiplexer_2 (
    .in0(PC_4), .in1(multiplexer_1_out), .out(NPC), .sel(and_1_out));
  or or_1 (BJRst, J, bJump);

  assign Jrst = J;
endmodule

module \气泡流水线  (
  output RegWrite,
  output MemWrite,
  output [31:0] IF_PC,
  output [31:0] ID_PC,
  output [31:0] EX_PC,
  output [31:0] M_PC,
  output [31:0] WB_PC,
  output [31:0] RDin,
  output [31:0] MDin,
  output [31:0] LedData
);

  wire CLK, clock_2_out, comparator_1_eq, comparator_1_lt, d_ff_1_q, Go, IR1, IR2, IR3, nand_1_out, RST, W1,
       W2, W3;
  wire [12:0] CNT_num;
  wire [15:0] \LoadUse次数 , \总周期数 , \插入气泡数 , \无条件分支数 , \条件分支成功数 ;
  wire [31:0] EX_IR, ID_IR, IF_IR, MEM_IR, WB_IR;

  Button \u_总复位  (.out(RST));
  Button _1 (.out(IR1));
  Button _2 (.out(IR2));
  Button _3 (.out(IR3));
  // Probe on \总周期数 
  // Probe on \总周期数 
  Button \u_继续运行  (.out(Go));
  LED #(.active("true")) led_1 (.in(W1));
  LED #(.active("true")) led_2 (.in(W2));
  LED #(.active("true")) led_3 (.in(W3));
  Hex_Digit_Display hex_digit_display_1 (.value(LedData[31:28]));  // open: dp
  // Probe on IF_PC[19:0]
  // RiscV_Probe riscv_probe_1: pin names not known; wires that end beside it: IF_IR
  Hex_Digit_Display hex_digit_display_2 (.value(LedData[27:24]));  // open: dp
  Hex_Digit_Display hex_digit_display_3 (.value(LedData[23:20]));  // open: dp
  // Probe on ID_PC[19:0]
  // RiscV_Probe riscv_probe_2: pin names not known; wires that end beside it: ID_IR
  Hex_Digit_Display hex_digit_display_4 (.value(LedData[15:12]));  // open: dp
  Hex_Digit_Display hex_digit_display_5 (.value(LedData[19:16]));  // open: dp
  Hex_Digit_Display hex_digit_display_6 (.value(LedData[11:8]));  // open: dp
  Hex_Digit_Display hex_digit_display_7 (.value(LedData[7:4]));  // open: dp
  Clock #(.highDuration(1), .lowDuration(1)) clock_1 (.out(CLK));
  // Probe on EX_PC[19:0]
  // RiscV_Probe riscv_probe_3: pin names not known; wires that end beside it: EX_IR
  Hex_Digit_Display hex_digit_display_8 (.value(LedData[3:0]));  // open: dp
  // Probe on \总周期数 
  // Probe on M_PC[19:0]
  // RiscV_Probe riscv_probe_4: pin names not known; wires that end beside it: MEM_IR
  // Probe on \总周期数 
  // Probe on \无条件分支数 
  // Probe on \条件分支成功数 
  // Probe on \插入气泡数 
  // Probe on \LoadUse次数 
  // Probe on IF_PC[11:0]
  // Probe on WB_PC[19:0]
  // RiscV_Probe riscv_probe_5: pin names not known; wires that end beside it: WB_IR
  // Probe on EX_PC[11:0]
  // Probe on ID_PC[11:0]
  // Probe on M_PC[11:0]
  D_Flip_Flop #(.trigger("high"), .Pre_Clr_Positions("LEGACY"), .NegatePresetClear("false"), .enable("true"), .NewFFLayout("false")) d_ff_1 (.Q(d_ff_1_q));  // open: clk, D, Qn, preset, en, reset
  // Probe on 13'hc
  // Probe on WB_PC[11:0]
  Comparator #(.width(13), .mode("twosComplement")) comparator_1 (
    .a(CNT_num), .b(13'hc), .eq(comparator_1_eq), .lt(comparator_1_lt));  // open: gt
  Clock #(.highDuration(1), .lowDuration(1)) clock_2 (.out(clock_2_out));
  nand nand_1 (nand_1_out, d_ff_1_q, comparator_1_eq);
  Counter #(.width(13), .max('h1fff), .ongoal("stay"), .trigger("rising"), .behavior("old")) counter_1 (
    .count(comparator_1_lt), .Q(CNT_num), .clk(clock_2_out));  // open: load, D, carry, clr, preset
  assign CLK = nand_1_out ? clock_2_out : 1'bz;  // Controlled_Buffer controlled_buffer_1
  Pull_Resistor #(.pull(1)) pull_resistor_1 (.node(CLK));

  // Other names for the same wires on the sheet: MEM_PC[31:0] = M_PC

  // Notes on the sheet:
  //   中断源
  //   时空图监测，可删除
  //   中断等待指示
  //   数码管输出
  //   控制位
  //   流水调试日志用
  //   暂停节拍，不能为0
  //   戳工具置1进入计数暂停模式，ctrl+k时钟自动运行到对应节拍暂停
  //   ctrl+k关闭时钟连续运行，将控制位置零，进入单步调试模式调试
  //   可计数暂停的时钟源
  //   为方便自动评测，需要输出流水线各段保存的PC值，注意是PC不是PC+4，另外ID段寄存器写入信息，Mem段内存写入信息也要输出
endmodule

module \重定向流水线  (
  output RegWrite,
  output MemWrite,
  output [31:0] IF_PC,
  output [31:0] ID_PC,
  output [31:0] EX_PC,
  output [31:0] M_PC,
  output [31:0] WB_PC,
  output [31:0] RDin,
  output [31:0] MDin,
  output [31:0] LedData
);

  wire CLK, clock_2_out, comparator_1_eq, comparator_1_lt, d_ff_1_q, Go, IR1, IR2, IR3, nand_1_out, RST, W1,
       W2, W3;
  wire [12:0] CNT_num;
  wire [15:0] \LoadUse次数 , \总周期数 , \插入气泡数 , \无条件分支数 , \条件分支成功数 ;
  wire [31:0] EX_IR, ID_IR, IF_IR, MEM_IR, WB_IR;

  Button \u_总复位  (.out(RST));
  Button _1 (.out(IR1));
  Button _2 (.out(IR2));
  Button _3 (.out(IR3));
  // Probe on \总周期数 
  // Probe on \总周期数 
  Button \u_继续运行  (.out(Go));
  LED #(.active("true")) led_1 (.in(W1));
  LED #(.active("true")) led_2 (.in(W2));
  LED #(.active("true")) led_3 (.in(W3));
  Hex_Digit_Display hex_digit_display_1 (.value(LedData[31:28]));  // open: dp
  // Probe on IF_PC[19:0]
  // RiscV_Probe riscv_probe_1: pin names not known; wires that end beside it: IF_IR
  Hex_Digit_Display hex_digit_display_2 (.value(LedData[23:20]));  // open: dp
  Hex_Digit_Display hex_digit_display_3 (.value(LedData[27:24]));  // open: dp
  // Probe on ID_PC[19:0]
  // RiscV_Probe riscv_probe_2: pin names not known; wires that end beside it: ID_IR
  Hex_Digit_Display hex_digit_display_4 (.value(LedData[19:16]));  // open: dp
  Hex_Digit_Display hex_digit_display_5 (.value(LedData[15:12]));  // open: dp
  Hex_Digit_Display hex_digit_display_6 (.value(LedData[7:4]));  // open: dp
  Hex_Digit_Display hex_digit_display_7 (.value(LedData[11:8]));  // open: dp
  Clock #(.highDuration(1), .lowDuration(1)) clock_1 (.out(CLK));
  // Probe on EX_PC[19:0]
  // RiscV_Probe riscv_probe_3: pin names not known; wires that end beside it: EX_IR
  Hex_Digit_Display hex_digit_display_8 (.value(LedData[3:0]));  // open: dp
  // Probe on \总周期数 
  // Probe on M_PC[19:0]
  // RiscV_Probe riscv_probe_4: pin names not known; wires that end beside it: MEM_IR
  // Probe on \总周期数 
  // Probe on \无条件分支数 
  // Probe on \条件分支成功数 
  // Probe on \插入气泡数 
  // Probe on \LoadUse次数 
  // Probe on IF_PC[11:0]
  // Probe on WB_PC[19:0]
  // RiscV_Probe riscv_probe_5: pin names not known; wires that end beside it: WB_IR
  // Probe on EX_PC[11:0]
  // Probe on ID_PC[11:0]
  // Probe on M_PC[11:0]
  D_Flip_Flop #(.trigger("high"), .Pre_Clr_Positions("LEGACY"), .NegatePresetClear("false"), .enable("true"), .NewFFLayout("false")) d_ff_1 (.Q(d_ff_1_q));  // open: clk, D, Qn, preset, en, reset
  // Probe on 13'hc
  // Probe on WB_PC[11:0]
  Comparator #(.width(13), .mode("twosComplement")) comparator_1 (
    .a(CNT_num), .b(13'hc), .eq(comparator_1_eq), .lt(comparator_1_lt));  // open: gt
  Clock #(.highDuration(1), .lowDuration(1)) clock_2 (.out(clock_2_out));
  nand nand_1 (nand_1_out, d_ff_1_q, comparator_1_eq);
  Counter #(.width(13), .max('h1fff), .ongoal("stay"), .trigger("rising"), .behavior("old")) counter_1 (
    .count(comparator_1_lt), .Q(CNT_num), .clk(clock_2_out));  // open: load, D, carry, clr, preset
  assign CLK = nand_1_out ? clock_2_out : 1'bz;  // Controlled_Buffer controlled_buffer_1
  Pull_Resistor #(.pull(1)) pull_resistor_1 (.node(CLK));

  // Other names for the same wires on the sheet: MEM_PC[31:0] = M_PC

  // Notes on the sheet:
  //   中断源
  //   时空图监测，可删除
  //   中断等待指示
  //   数码管输出
  //   控制位
  //   流水调试日志用
  //   暂停节拍，不能为0
  //   戳工具置1进入计数暂停模式，ctrl+k时钟自动运行到对应节拍暂停
  //   ctrl+k关闭时钟连续运行，将控制位置零，进入单步调试模式调试
  //   可计数暂停的时钟源
  //   为方便自动评测，需要输出流水线各段保存的PC值，注意是PC不是PC+4，另外ID段寄存器写入信息，Mem段内存写入信息也要输出
endmodule

module \中断按键参考电路  (
  input  \同步清零信号 ,
  output \与中断屏蔽位与 
);

  wire \_1号中断_out , and_1_out, clock_1_out, d_ff_1_q, or_1_out, or_2_out;

  Clock #(.highDuration(1), .lowDuration(1)) clock_1 (.out(clock_1_out));
  Button \_1号中断  (.out(\_1号中断_out ));
  or or_1 (or_1_out, \与中断屏蔽位与 , d_ff_1_q);
  LED #(.active("true")) \_1号中断等待指示灯  (.in(or_1_out));
  D_Flip_Flop #(.trigger("rising"), .Pre_Clr_Positions("LEGACY"), .NegatePresetClear("false"), .enable("true"), .NewFFLayout("false")) d_ff_1 (
    .clk(\_1号中断_out ), .D(1'b1), .Q(d_ff_1_q), .reset(\与中断屏蔽位与 ));  // open: Qn, preset, en
  or or_2 (or_2_out, d_ff_1_q, \与中断屏蔽位与 );
  and and_1 (and_1_out, or_2_out, ~\同步清零信号 );  // AND_Gate
  D_Flip_Flop #(.trigger("rising"), .Pre_Clr_Positions("LEGACY"), .NegatePresetClear("false"), .enable("true"), .NewFFLayout("false")) IR1 (
    .clk(clock_1_out), .D(and_1_out), .Q(\与中断屏蔽位与 ));  // open: Qn, preset, en, reset

  // Notes on the sheet:
  //   中断信号采样参考电路
  //   Reset 
endmodule

module \单周期_单级中断  (
  input  IR1,
  input  IR2,
  input  IR3,
  output RegWrite,
  output MemWrite,
  output [31:0] PC,
  output [31:0] IR,
  output [31:0] RDin,
  output [31:0] MDin,
  output [31:0] LedData
);

  wire CLK, comparator_1_eq, comparator_2_eq, comparator_3_eq, comparator_4_eq, Go, IR1_t, IR2_t, IR3_t, IRA,
       IRB, IRC, or_1_out, W1, W2, W3;
  wire [15:0] \总周期数 ;

  Clock #(.highDuration(1), .lowDuration(1)) clock_1 (.out(CLK));
  Button _1 ();  // open: out
  Button _2 ();  // open: out
  Button _3 ();  // open: out
  Button \u_继续运行  (.out(Go));
  LED #(.active("true")) led_1 (.in(W1));
  LED #(.active("true")) led_2 (.in(W2));
  LED #(.active("true")) led_3 (.in(W3));
  Hex_Digit_Display hex_digit_display_1 (.value(LedData[31:28]));  // open: dp
  Comparator #(.width(16), .mode("twosComplement")) comparator_1 (
    .a(16'h23b), .b(\总周期数 ), .eq(comparator_1_eq));  // open: gt, lt
  Comparator #(.width(16), .mode("twosComplement")) comparator_2 (
    .a(\总周期数 ), .b(16'h1), .eq(comparator_2_eq));  // open: gt, lt
  Comparator #(.width(16), .mode("twosComplement")) comparator_3 (
    .a(\总周期数 ), .b(16'h4), .eq(comparator_3_eq));  // open: gt, lt
  Comparator #(.width(16), .mode("twosComplement")) comparator_4 (
    .a(\总周期数 ), .b(16'h7), .eq(comparator_4_eq));  // open: gt, lt
  Hex_Digit_Display hex_digit_display_2 (.value(LedData[27:24]));  // open: dp
  Hex_Digit_Display hex_digit_display_3 (.value(LedData[23:20]));  // open: dp
  or or_1 (or_1_out, comparator_1_eq, comparator_2_eq);
  assign IRA = or_1_out ? ~CLK : 1'bz;  // Controlled_Inverter controlled_inverter_1
  assign IRB = comparator_3_eq ? ~CLK : 1'bz;  // Controlled_Inverter controlled_inverter_2
  assign IRC = comparator_4_eq ? ~CLK : 1'bz;  // Controlled_Inverter controlled_inverter_3
  Hex_Digit_Display hex_digit_display_4 (.value(LedData[15:12]));  // open: dp
  Hex_Digit_Display hex_digit_display_5 (.value(LedData[19:16]));  // open: dp
  Pull_Resistor #(.pull(0)) pull_resistor_1 (.node(IRA));
  Pull_Resistor #(.pull(0)) pull_resistor_2 (.node(IRB));
  Pull_Resistor #(.pull(0)) pull_resistor_3 (.node(IRC));
  Hex_Digit_Display hex_digit_display_6 (.value(LedData[7:4]));  // open: dp
  Hex_Digit_Display hex_digit_display_7 (.value(LedData[11:8]));  // open: dp
  // Probe on \总周期数 
  Hex_Digit_Display hex_digit_display_8 (.value(LedData[3:0]));  // open: dp
  or or_2 (IR1_t, IR1, IRA);
  or or_3 (IR2_t, IR2, IRB);
  or or_4 (IR3_t, IR3, IRC);

  // Notes on the sheet:
  //   中断源
  //   中断等待指示
  //   总复位信号应将除ROM以外所有存储组件全部清零
  //   单级中断测试信号模拟器
  //   数码管输出
  //   数码管输出应该用寄存器锁存，否则显示数据只能一闪而过
  //   为方便自动评测，需要输出PC，IR，寄存器堆写如数据RDin
  //   RAM写使能MemWrite、RAM写入数据MDin等信号
endmodule

module \单周期_多级中断  (
  input  IR1,
  input  IR2,
  input  IR3,
  output RegWrite,
  output MemWrite,
  output [31:0] PC,
  output [31:0] IR,
  output [31:0] RDin,
  output [31:0] MDin,
  output [31:0] LedData
);

  wire CLK, comparator_1_eq, comparator_2_eq, comparator_3_eq, comparator_4_eq, comparator_5_eq, Go, IR1_t,
       IR2_t, IR3_t, IRA, IRB, IRC, or_1_out, or_2_out, W1, W2, W3;
  wire [15:0] \总周期数 ;

  Clock #(.highDuration(1), .lowDuration(1)) clock_1 (.out(CLK));
  Button _1 ();  // open: out
  Button _2 ();  // open: out
  Button _3 ();  // open: out
  Button \u_继续运行  (.out(Go));
  LED #(.active("true")) led_1 (.in(W1));
  LED #(.active("true")) led_2 (.in(W2));
  LED #(.active("true")) led_3 (.in(W3));
  Hex_Digit_Display hex_digit_display_1 (.value(LedData[31:28]));  // open: dp
  Comparator #(.width(16), .mode("twosComplement")) comparator_1 (
    .a(\总周期数 ), .b(16'h7), .eq(comparator_1_eq));  // open: gt, lt
  Comparator #(.width(16), .mode("twosComplement")) comparator_2 (
    .a(\总周期数 ), .b(16'h241), .eq(comparator_2_eq));  // open: gt, lt
  Hex_Digit_Display hex_digit_display_2 (.value(LedData[23:20]));  // open: dp
  Hex_Digit_Display hex_digit_display_3 (.value(LedData[27:24]));  // open: dp
  Comparator #(.width(16), .mode("twosComplement")) comparator_3 (
    .a(16'h258), .b(\总周期数 ), .eq(comparator_3_eq));  // open: gt, lt
  or or_1 (or_1_out, comparator_3_eq, comparator_4_eq);
  Comparator #(.width(16), .mode("twosComplement")) comparator_4 (
    .a(\总周期数 ), .b(16'h1), .eq(comparator_4_eq));  // open: gt, lt
  Comparator #(.width(16), .mode("twosComplement")) comparator_5 (
    .a(\总周期数 ), .b(16'h4), .eq(comparator_5_eq));  // open: gt, lt
  or or_2 (or_2_out, comparator_1_eq, comparator_2_eq);
  Hex_Digit_Display hex_digit_display_4 (.value(LedData[19:16]));  // open: dp
  Hex_Digit_Display hex_digit_display_5 (.value(LedData[15:12]));  // open: dp
  Pull_Resistor #(.pull(0)) pull_resistor_1 (.node(IRA));
  assign IRA = or_1_out ? ~CLK : 1'bz;  // Controlled_Inverter controlled_inverter_1
  Pull_Resistor #(.pull(0)) pull_resistor_2 (.node(IRB));
  assign IRB = comparator_5_eq ? ~CLK : 1'bz;  // Controlled_Inverter controlled_inverter_2
  Pull_Resistor #(.pull(0)) pull_resistor_3 (.node(IRC));
  assign IRC = or_2_out ? ~CLK : 1'bz;  // Controlled_Inverter controlled_inverter_3
  Hex_Digit_Display hex_digit_display_6 (.value(LedData[11:8]));  // open: dp
  Hex_Digit_Display hex_digit_display_7 (.value(LedData[7:4]));  // open: dp
  // Probe on \总周期数 
  Hex_Digit_Display hex_digit_display_8 (.value(LedData[3:0]));  // open: dp
  or or_3 (IR1_t, IR1, IRA);
  or or_4 (IR2_t, IR2, IRB);
  or or_5 (IR3_t, IR3, IRC);

  // Notes on the sheet:
  //   中断源
  //   中断等待指示
  //   总复位信号应将除ROM以外所有存储组件全部清零
  //   多级中断测试信号模拟器
  //   数码管输出
  //   数码管输出应该用寄存器锁存，否则显示数据只能一闪而过
  //   为方便自动评测，需要输出PC，IR，寄存器堆写如数据RDin
  //   RAM写使能MemWrite、RAM写入数据MDin等信号
endmodule

module \封装正确性测试  (
);

  wire IR1, IR2, IR3, MemW, RegW;
  wire [31:0] EX_PC, ID_PC, IF_PC, IR, LED, MDin, MDinr, MEM_PC, PC, RDin, RDinr, WB_PC;

  \单周期RISC_V  \u_单周期risc_v_1  (
    .IR1(IR1), .IR2(IR2), .IR3(IR3), .RegWrite(RegW), .MemWrite(MemW), .PC(PC), .IR(IR), .RDin(RDin),
    .MDin(MDin), .LedData(LED));
  \气泡流水线  \u_气泡流水线_1  (
    .RegWrite(RegW), .MemWrite(MemW), .IF_PC(IF_PC), .ID_PC(ID_PC), .EX_PC(EX_PC), .M_PC(MEM_PC),
    .WB_PC(WB_PC), .RDin(RDinr), .MDin(MDinr), .LedData(LED));
  \单周期_单级中断  \u_单周期_单级中断_1  (
    .IR1(IR1), .IR2(IR2), .IR3(IR3), .RegWrite(RegW), .MemWrite(MemW), .PC(PC), .IR(IR), .RDin(RDin),
    .MDin(MDin), .LedData(LED));
  \理想流水线  \u_理想流水线_1  (
    .RegWrite(RegW), .MemWrite(MemW), .IF_PC(IF_PC), .ID_PC(ID_PC), .EX_PC(EX_PC), .M_PC(MEM_PC),
    .WB_PC(WB_PC), .RDin(RDinr), .MDin(MDinr), .LedData(LED));
  \重定向流水线  \u_重定向流水线_1  (
    .RegWrite(RegW), .MemWrite(MemW), .IF_PC(IF_PC), .ID_PC(ID_PC), .EX_PC(EX_PC), .M_PC(MEM_PC),
    .WB_PC(WB_PC), .RDin(RDinr), .MDin(MDinr), .LedData(LED));
  \单周期_多级中断  \u_单周期_多级中断_1  (
    .IR1(IR1), .IR2(IR2), .IR3(IR3), .RegWrite(RegW), .MemWrite(MemW), .PC(PC), .IR(IR), .RDin(RDin),
    .MDin(MDin), .LedData(LED));

  // Notes on the sheet:
  //   单周期封装测试
  //   气泡流水封装测试
  //   单周期+单级中断封装测试
  //   请检查上面封装有无位宽不匹配，引脚标签是否和连接的标签相对应，否则无法在educoder平台上正确测试
  //   理想流水封装测试
  //   重定向流水封装测试
  //   单周期+多级中断封装测试
endmodule
